// Digital circuit 16_bit_reg_cnt.dig as structural Verilog
module _16_bit_reg_cnt (
  input  LOW_D,
  input  HIGH_D,
  input  OUT_A,
  input  LOW_LD,
  input  HIGH_LD,
  input  INC,
  input  DEC,
  input  RST,
  input  [7:0] DATA,
  output [7:0] DATA_OUT,
  output [15:0] Address,
  output [15:0] DBG
);

  wire _74193_1_pin12, _74193_1_pin13, _74193_2_pin12, _74193_2_pin13, _74193_3_pin12, _74193_3_pin13;

  _74193 _74193_1 (
    .pin1(DATA[1]), .pin2(DBG[1]), .pin3(DBG[0]), .pin4(DEC), .pin5(INC), .pin6(DBG[2]), .pin7(DBG[3]),
    .pin8(1'b0), .pin9(DATA[3]), .pin10(DATA[2]), .pin11(LOW_LD), .pin12(_74193_1_pin12),
    .pin13(_74193_1_pin13), .pin14(RST), .pin15(DATA[0]), .pin16(1'b1));
  _74193 _74193_2 (
    .pin1(DATA[5]), .pin2(DBG[5]), .pin3(DBG[4]), .pin4(_74193_1_pin13), .pin5(_74193_1_pin12),
    .pin6(DBG[6]), .pin7(DBG[7]), .pin8(1'b0), .pin9(DATA[7]), .pin10(DATA[6]), .pin11(LOW_LD),
    .pin12(_74193_2_pin12), .pin13(_74193_2_pin13), .pin14(RST), .pin15(DATA[4]), .pin16(1'b1));
  _74541 _74541_1 (
    .pin1(1'b0), .pin2(DBG[0]), .pin3(DBG[1]), .pin4(DBG[2]), .pin5(DBG[3]), .pin6(DBG[4]), .pin7(DBG[5]),
    .pin8(DBG[6]), .pin9(DBG[7]), .pin10(1'b0), .pin11(DATA_OUT[7]), .pin12(DATA_OUT[6]),
    .pin13(DATA_OUT[5]), .pin14(DATA_OUT[4]), .pin15(DATA_OUT[3]), .pin16(DATA_OUT[2]), .pin17(DATA_OUT[1]),
    .pin18(DATA_OUT[0]), .pin19(LOW_D), .pin20(1'b1));
  _74193 _74193_3 (
    .pin1(DATA[1]), .pin2(DBG[9]), .pin3(DBG[8]), .pin4(_74193_2_pin13), .pin5(_74193_2_pin12),
    .pin6(DBG[10]), .pin7(DBG[11]), .pin8(1'b0), .pin9(DATA[3]), .pin10(DATA[2]), .pin11(HIGH_LD),
    .pin12(_74193_3_pin12), .pin13(_74193_3_pin13), .pin14(RST), .pin15(DATA[0]), .pin16(1'b1));
  _74193 _74193_4 (
    .pin1(DATA[5]), .pin2(DBG[13]), .pin3(DBG[12]), .pin4(_74193_3_pin13), .pin5(_74193_3_pin12),
    .pin6(DBG[14]), .pin7(DBG[15]), .pin8(1'b0), .pin9(DATA[7]), .pin10(DATA[6]), .pin11(HIGH_LD),
    .pin14(RST), .pin15(DATA[4]), .pin16(1'b1));  // open: pin12, pin13
  _74541 _74541_2 (
    .pin1(1'b0), .pin2(DBG[8]), .pin3(DBG[9]), .pin4(DBG[10]), .pin5(DBG[11]), .pin6(DBG[12]),
    .pin7(DBG[13]), .pin8(DBG[14]), .pin9(DBG[15]), .pin10(1'b0), .pin11(DATA_OUT[7]), .pin12(DATA_OUT[6]),
    .pin13(DATA_OUT[5]), .pin14(DATA_OUT[4]), .pin15(DATA_OUT[3]), .pin16(DATA_OUT[2]), .pin17(DATA_OUT[1]),
    .pin18(DATA_OUT[0]), .pin19(HIGH_D), .pin20(1'b1));
  _74541 _74541_3 (
    .pin1(1'b0), .pin2(DBG[8]), .pin3(DBG[9]), .pin4(DBG[10]), .pin5(DBG[11]), .pin6(DBG[12]),
    .pin7(DBG[13]), .pin8(DBG[14]), .pin9(DBG[15]), .pin10(1'b0), .pin11(Address[15]), .pin12(Address[14]),
    .pin13(Address[13]), .pin14(Address[12]), .pin15(Address[11]), .pin16(Address[10]), .pin17(Address[9]),
    .pin18(Address[8]), .pin19(OUT_A), .pin20(1'b1));
  _74541 _74541_4 (
    .pin1(1'b0), .pin2(DBG[0]), .pin3(DBG[1]), .pin4(DBG[2]), .pin5(DBG[3]), .pin6(DBG[4]), .pin7(DBG[5]),
    .pin8(DBG[6]), .pin9(DBG[7]), .pin10(1'b0), .pin11(Address[7]), .pin12(Address[6]), .pin13(Address[5]),
    .pin14(Address[4]), .pin15(Address[3]), .pin16(Address[2]), .pin17(Address[1]), .pin18(Address[0]),
    .pin19(OUT_A), .pin20(1'b1));

  // Notes on the sheet:
  //   LOW_D: default 1
  //   HIGH_D: default 1
  //   OUT_A: default 1
  //   LOW_LD: default 1
  //   HIGH_LD: default 1
endmodule
