// Digital circuit MMU.dig as structural Verilog
module MMU (
  input  [7:0] DATA,
  input  [15:0] ADDRESS,
  input  MREAD,
  input  MWRITE,
  input  [7:0] IN_0,
  input  [7:0] IN_1,
  input  [7:0] IN_2,
  input  [7:0] IN_3,
  input  [7:0] IN_4,
  input  [7:0] IN_5,
  input  [7:0] IN_6,
  input  INT_0_EDGE,
  input  INT_1_EDGE,
  input  INT_2_EDGE,
  input  INT_3_LEVEL,
  input  P0,
  input  RST,
  input  iv_o,
  input  ei,
  input  pg_dis,
  output [7:0] LED_R0,
  output [7:0] LED_R1,
  output [7:0] LED_R2,
  output [7:0] LED_R3,
  output [7:0] LED_R4,
  output [7:0] LED_R5,
  output [7:0] LED_R6,
  output [7:0] LED_R7,
  output IRQ,
  output TERM_SEL,
  output DBG_int_enabled,
  output [7:0] DBG_TLB_index,
  output STORAGE_SEL
);

  wire _74138_1_pin12, _74138_1_pin13, _74138_1_pin14, _74138_1_pin15, _74138_2_pin13, _74138_2_pin14,
       _74138_2_pin15, _74138_3_pin7, _74138_3_pin9, _74138_3_pin10, _74138_3_pin11, _74138_3_pin12,
       _74138_3_pin13, _74138_3_pin14, _74138_3_pin15, _74138_4_pin7, _74138_4_pin9, _74138_4_pin10,
       _74138_4_pin11, _74138_4_pin12, _74138_4_pin13, _74138_4_pin14, _74138_4_pin15, _74138_5_pin13,
       _74138_5_pin14, _74138_5_pin15, _74573_1_pin11, _74573_2_pin1, _74573_8_pin16, _74573_8_pin17,
       _74573_8_pin18, _74573_8_pin19, and_1_out, and_2_out, and_3_out, and_4_out, and_5_out, and_6_out,
       and_7_out, and_8_out, and_9_out, and_10_out, and_11_out, and_12_out, and_13_out, and_14_out,
       and_15_out, nor_2_out, nor_3_out, nor_4_out, nor_5_out, nor_6_out, nor_7_out, nor_8_out, nor_9_out,
       nor_11_out, not_1_out, not_2_out, not_3_out, not_5_out, not_6_out, not_7_out, not_8_out, not_9_out,
       not_10_out, not_11_out, not_12_out, not_13_out, not_14_out, not_15_out, not_16_out, not_17_out,
       not_18_out, not_19_out, not_20_out, not_21_out, not_22_out, not_23_out, not_24_out, or_1_out,
       or_2_out, or_3_out, or_4_out, or_5_out, or_6_out, or_7_out, or_8_out, or_9_out, or_10_out, or_11_out,
       or_12_out, or_13_out, or_14_out, or_15_out, or_16_out, or_17_out, or_18_out, or_19_out, or_20_out,
       or_21_out, or_22_out, or_23_out, or_24_out, or_25_out, or_26_out, or_27_out;
  wire [7:0] _74573_3_pin2, TLBFlags_d;
  wire [11:0] _74573_4_pin19;
  wire [15:12] _74573_2_pin16;
  wire [19:16] _74573_2_pin12;

  not not_1 (not_1_out, _74573_2_pin1);
  not not_2 (not_2_out, ADDRESS[0]);
  _74573 _74573_1 (
    .pin1(not_1_out), .pin2(DATA[0]), .pin3(DATA[1]), .pin4(DATA[2]), .pin5(DATA[3]), .pin6(DATA[4]),
    .pin7(DATA[5]), .pin8(DATA[6]), .pin9(DATA[7]), .pin10(1'b0), .pin11(_74573_1_pin11),
    .pin12(DBG_TLB_index[7]), .pin13(DBG_TLB_index[6]), .pin14(DBG_TLB_index[5]), .pin15(DBG_TLB_index[4]),
    .pin16(DBG_TLB_index[3]), .pin17(DBG_TLB_index[2]), .pin18(DBG_TLB_index[1]), .pin19(DBG_TLB_index[0]),
    .pin20(1'b1));
  not not_3 (not_3_out, or_5_out);
  and and_1 (and_1_out, not_2_out, not_3_out);
  and and_2 (and_2_out, ADDRESS[0], not_3_out);
  PullDown pulldown_1 (.out(DBG_TLB_index[0]));
  PullDown pulldown_2 (.out(DBG_TLB_index[1]));
  not not_4 (_74573_1_pin11, or_3_out);
  not not_5 (not_5_out, ei);
  PullDown pulldown_3 (.out(DBG_TLB_index[2]));
  PullDown pulldown_4 (.out(DBG_TLB_index[3]));
  PullDown pulldown_5 (.out(DBG_TLB_index[4]));
  PullDown pulldown_6 (.out(DBG_TLB_index[5]));
  or or_1 (or_1_out, pg_dis, and_1_out);
  or or_2 (or_2_out, not_5_out, and_2_out);
  not not_6 (not_6_out, _74573_2_pin1);
  PullDown pulldown_7 (.out(DBG_TLB_index[6]));
  PullDown pulldown_8 (.out(DBG_TLB_index[7]));
  or or_3 (or_3_out, _74138_5_pin13, MWRITE);
  _74573 _74573_2 (
    .pin1(_74573_2_pin1), .pin2(ADDRESS[12]), .pin3(ADDRESS[13]), .pin4(ADDRESS[14]), .pin5(ADDRESS[15]),
    .pin6(1'b0), .pin7(1'b0), .pin8(1'b0), .pin9(1'b0), .pin10(1'b0), .pin11(1'b1),
    .pin12(_74573_2_pin12[19]), .pin13(_74573_2_pin12[18]), .pin14(_74573_2_pin12[17]),
    .pin15(_74573_2_pin12[16]), .pin16(_74573_2_pin16[15]), .pin17(_74573_2_pin16[14]),
    .pin18(_74573_2_pin16[13]), .pin19(_74573_2_pin16[12]), .pin20(1'b1));
  or or_4 (or_4_out, RST, or_1_out);
  _74573 _74573_3 (
    .pin1(not_6_out), .pin2(_74573_3_pin2[0]), .pin3(_74573_3_pin2[1]), .pin4(_74573_3_pin2[2]),
    .pin5(_74573_3_pin2[3]), .pin6(_74573_3_pin2[4]), .pin7(_74573_3_pin2[5]), .pin8(_74573_3_pin2[6]),
    .pin9(_74573_3_pin2[7]), .pin10(1'b0), .pin11(1'b1), .pin12(_74573_2_pin12[19]),
    .pin13(_74573_2_pin12[18]), .pin14(_74573_2_pin12[17]), .pin15(_74573_2_pin12[16]),
    .pin16(_74573_2_pin16[15]), .pin17(_74573_2_pin16[14]), .pin18(_74573_2_pin16[13]),
    .pin19(_74573_2_pin16[12]), .pin20(1'b1));
  nor nor_1 (_74573_2_pin1, or_4_out, nor_2_out);
  nor nor_2 (nor_2_out, _74573_2_pin1, or_2_out);
  _74573 _74573_4 (
    .pin1(not_6_out), .pin2(ADDRESS[12]), .pin3(ADDRESS[13]), .pin4(ADDRESS[14]), .pin5(ADDRESS[15]),
    .pin6(DBG_TLB_index[0]), .pin7(DBG_TLB_index[1]), .pin8(DBG_TLB_index[2]), .pin9(DBG_TLB_index[3]),
    .pin10(1'b0), .pin11(1'b1), .pin12(_74573_4_pin19[7]), .pin13(_74573_4_pin19[6]),
    .pin14(_74573_4_pin19[5]), .pin15(_74573_4_pin19[4]), .pin16(_74573_4_pin19[3]),
    .pin17(_74573_4_pin19[2]), .pin18(_74573_4_pin19[1]), .pin19(_74573_4_pin19[0]), .pin20(1'b1));
  _74573 _74573_5 (
    .pin1(not_6_out), .pin2(DBG_TLB_index[4]), .pin3(DBG_TLB_index[5]), .pin4(DBG_TLB_index[6]),
    .pin5(DBG_TLB_index[7]), .pin6(1'b0), .pin7(1'b0), .pin8(1'b0), .pin9(1'b0), .pin10(1'b0), .pin11(1'b1),
    .pin16(_74573_4_pin19[11]), .pin17(_74573_4_pin19[10]), .pin18(_74573_4_pin19[9]),
    .pin19(_74573_4_pin19[8]), .pin20(1'b1));  // open: pin12, pin13, pin14, pin15
  or or_5 (or_5_out, MWRITE, and_15_out);
  _74573 _74573_6 (
    .pin1(_74573_2_pin1), .pin2(ADDRESS[0]), .pin3(ADDRESS[1]), .pin4(ADDRESS[2]), .pin5(ADDRESS[3]),
    .pin6(ADDRESS[4]), .pin7(ADDRESS[5]), .pin8(ADDRESS[6]), .pin9(ADDRESS[7]), .pin10(1'b0), .pin11(1'b1),
    .pin12(_74573_4_pin19[7]), .pin13(_74573_4_pin19[6]), .pin14(_74573_4_pin19[5]),
    .pin15(_74573_4_pin19[4]), .pin16(_74573_4_pin19[3]), .pin17(_74573_4_pin19[2]),
    .pin18(_74573_4_pin19[1]), .pin19(_74573_4_pin19[0]), .pin20(1'b1));
  _74573 _74573_7 (
    .pin1(_74573_2_pin1), .pin2(ADDRESS[8]), .pin3(ADDRESS[9]), .pin4(ADDRESS[10]), .pin5(ADDRESS[11]),
    .pin6(1'b0), .pin7(1'b0), .pin8(1'b0), .pin9(1'b0), .pin10(1'b0), .pin11(1'b1),
    .pin16(_74573_4_pin19[11]), .pin17(_74573_4_pin19[10]), .pin18(_74573_4_pin19[9]),
    .pin19(_74573_4_pin19[8]), .pin20(1'b1));  // open: pin12, pin13, pin14, pin15
  or or_6 (or_6_out, _74573_2_pin12[16], _74573_2_pin12[17]);
  or or_7 (or_7_out, _74573_2_pin12[18], _74573_2_pin12[19]);
  not not_7 (not_7_out, iv_o);
  and and_3 (and_3_out, _74573_8_pin19, not_7_out);
  and and_4 (and_4_out, _74573_8_pin18, not_7_out);
  and and_5 (and_5_out, _74573_8_pin17, not_7_out);
  or or_8 (or_8_out, or_6_out, or_7_out);
  or or_9 (or_9_out, and_3_out, RST);
  or or_10 (or_10_out, and_4_out, RST);
  or or_11 (or_11_out, and_5_out, RST);
  not not_8 (not_8_out, or_8_out);
  nor nor_3 (nor_3_out, or_9_out, nor_4_out);
  nor nor_4 (nor_4_out, nor_3_out, INT_0_EDGE);
  nor nor_5 (nor_5_out, or_10_out, nor_6_out);
  nor nor_6 (nor_6_out, nor_5_out, INT_1_EDGE);
  nor nor_7 (nor_7_out, or_11_out, nor_8_out);
  nor nor_8 (nor_8_out, nor_7_out, INT_2_EDGE);
  RAMSinglePortSel #(.AddrBits(20), .isProgramMemory("true"), .Bits(8)) ExtRam (
    .A({_74573_2_pin12, _74573_2_pin16, ADDRESS[11:0]}), .CS(or_8_out), .WE(not_10_out), .OE(not_9_out),
    .D(DATA));
  and and_6 (and_6_out, not_8_out, _74573_2_pin16[15]);
  _74138 _74138_1 (
    .pin1(_74573_2_pin16[13]), .pin2(_74573_2_pin16[14]), .pin3(_74573_2_pin16[15]), .pin4(or_8_out),
    .pin5(1'b0), .pin6(1'b1), .pin8(1'b0), .pin12(_74138_1_pin12), .pin13(_74138_1_pin13),
    .pin14(_74138_1_pin14), .pin15(_74138_1_pin15), .pin16(1'b1));  // open: pin7, pin9, pin10, pin11
  not not_9 (not_9_out, MREAD);
  not not_10 (not_10_out, MWRITE);
  not not_11 (not_11_out, nor_3_out);
  and and_7 (and_7_out, _74138_1_pin15, _74138_1_pin14);
  or or_12 (or_12_out, MREAD, or_14_out);
  and and_8 (and_8_out, not_11_out, nor_5_out);
  or or_13 (or_13_out, nor_3_out, nor_5_out);
  not not_12 (not_12_out, _74573_2_pin16[12]);
  or or_14 (or_14_out, _74138_1_pin12, not_12_out);
  or or_15 (or_15_out, MWRITE, or_14_out);
  not not_13 (not_13_out, or_13_out);
  RAMSinglePortSel #(.AddrBits(15), .isProgramMemory("true"), .Bits(8)) LowRam (
    .A({_74573_2_pin16[14:12], ADDRESS[11:0]}), .CS(and_6_out), .WE(not_14_out), .OE(not_15_out), .D(DATA));
  not not_14 (not_14_out, MWRITE);
  and and_9 (and_9_out, or_18_out, not_6_out);
  and and_10 (and_10_out, or_12_out, not_6_out);
  and and_11 (and_11_out, not_13_out, nor_7_out);
  or or_16 (or_16_out, or_13_out, nor_7_out);
  not not_15 (not_15_out, MREAD);
  or or_17 (or_17_out, _74138_1_pin12, _74573_2_pin16[12]);
  or or_18 (or_18_out, MREAD, or_17_out);
  not not_16 (not_16_out, ei);
  not not_17 (not_17_out, or_16_out);
  ROM #(.AddrBits(14), .isProgramMemory("true"), .Bits(8)) Rom (
    .A({_74573_2_pin16[13:12], ADDRESS[11:0]}), .sel(nor_9_out), .D(DATA));
  or or_19 (or_19_out, MWRITE, or_17_out);
  not not_18 (not_18_out, or_19_out);
  not not_19 (not_19_out, and_9_out);
  not not_20 (not_20_out, or_15_out);
  not not_21 (not_21_out, and_10_out);
  and and_12 (and_12_out, not_17_out, INT_3_LEVEL);
  nor nor_9 (nor_9_out, MREAD, and_7_out);
  RAMSinglePortSel #(.AddrBits(12), .isProgramMemory("true"), .Bits(8)) TLB (
    .A(_74573_4_pin19), .CS(1'b1), .WE(not_18_out), .OE(not_19_out), .D(_74573_3_pin2));
  RAMSinglePortSel #(.AddrBits(12), .isProgramMemory("true"), .Bits(8)) TLBFlags (
    .A(_74573_4_pin19), .CS(1'b1), .WE(not_20_out), .OE(not_21_out), .D(TLBFlags_d));
  _74573 _74573_8 (
    .pin1(1'b0), .pin2(nor_3_out), .pin3(and_8_out), .pin4(and_11_out), .pin5(and_12_out), .pin6(1'b0),
    .pin7(1'b0), .pin8(1'b0), .pin9(1'b0), .pin10(1'b0), .pin11(P0), .pin16(_74573_8_pin16),
    .pin17(_74573_8_pin17), .pin18(_74573_8_pin18), .pin19(_74573_8_pin19), .pin20(1'b1));  // open: pin12, pin13, pin14, pin15
  assign DATA = ~or_18_out ? _74573_3_pin2 : 8'bz;  // DriverInvSel driverinvsel_1
  assign _74573_3_pin2 = ~not_22_out ? DATA : 8'bz;  // DriverInvSel driverinvsel_2
  assign DATA = ~or_12_out ? TLBFlags_d : 8'bz;  // DriverInvSel driverinvsel_3
  assign TLBFlags_d = ~not_23_out ? DATA : 8'bz;  // DriverInvSel driverinvsel_4
  not not_22 (not_22_out, and_13_out);
  not not_23 (not_23_out, and_14_out);
  _74138 _74138_2 (
    .pin1(ADDRESS[10]), .pin2(ADDRESS[11]), .pin3(_74573_2_pin16[12]), .pin4(_74138_1_pin13), .pin5(1'b0),
    .pin6(1'b1), .pin8(1'b0), .pin13(_74138_2_pin13), .pin14(_74138_2_pin14), .pin15(_74138_2_pin15),
    .pin16(1'b1));  // open: pin7, pin9, pin10, pin11, pin12
  and and_13 (and_13_out, not_6_out, or_18_out);
  and and_14 (and_14_out, not_6_out, or_12_out);
  or or_20 (or_20_out, or_23_out, or_22_out);
  or or_21 (or_21_out, or_20_out, _74573_8_pin19);
  not not_24 (not_24_out, or_21_out);
  or or_22 (or_22_out, _74573_8_pin17, _74573_8_pin16);
  or or_23 (or_23_out, _74573_8_pin18, _74573_8_pin16);
  _74573 _74573_9 (
    .pin1(iv_o), .pin2(1'b0), .pin3(1'b0), .pin4(1'b0), .pin5(1'b0), .pin6(or_23_out), .pin7(or_22_out),
    .pin8(not_24_out), .pin9(1'b0), .pin10(1'b0), .pin11(1'b1), .pin12(DATA[7]), .pin13(DATA[6]),
    .pin14(DATA[5]), .pin15(DATA[4]), .pin16(DATA[3]), .pin17(DATA[2]), .pin18(DATA[1]), .pin19(DATA[0]),
    .pin20(1'b1));
  or or_24 (or_24_out, _74573_8_pin19, _74573_8_pin18);
  or or_25 (or_25_out, _74573_8_pin17, _74573_8_pin16);
  _74138 _74138_3 (
    .pin1(ADDRESS[0]), .pin2(ADDRESS[1]), .pin3(ADDRESS[2]), .pin4(_74138_2_pin15), .pin5(1'b0), .pin6(1'b1),
    .pin7(_74138_3_pin7), .pin8(1'b0), .pin9(_74138_3_pin9), .pin10(_74138_3_pin10), .pin11(_74138_3_pin11),
    .pin12(_74138_3_pin12), .pin13(_74138_3_pin13), .pin14(_74138_3_pin14), .pin15(_74138_3_pin15),
    .pin16(1'b1));
  _74138 _74138_4 (
    .pin1(ADDRESS[0]), .pin2(ADDRESS[1]), .pin3(ADDRESS[2]), .pin4(_74138_2_pin14), .pin5(MREAD),
    .pin6(1'b1), .pin7(_74138_4_pin7), .pin8(1'b0), .pin9(_74138_4_pin9), .pin10(_74138_4_pin10),
    .pin11(_74138_4_pin11), .pin12(_74138_4_pin12), .pin13(_74138_4_pin13), .pin14(_74138_4_pin14),
    .pin15(_74138_4_pin15), .pin16(1'b1));
  _74138 _74138_5 (
    .pin1(ADDRESS[0]), .pin2(ADDRESS[1]), .pin3(ADDRESS[2]), .pin4(_74138_2_pin13), .pin5(1'b0), .pin6(1'b1),
    .pin8(1'b0), .pin11(STORAGE_SEL), .pin12(TERM_SEL), .pin13(_74138_5_pin13), .pin14(_74138_5_pin14),
    .pin15(_74138_5_pin15), .pin16(1'b1));  // open: pin7, pin9, pin10
  or or_26 (or_26_out, RST, not_7_out);
  nor nor_10 (DBG_int_enabled, or_26_out, nor_11_out);
  nor nor_11 (nor_11_out, DBG_int_enabled, not_16_out);
  or or_27 (or_27_out, or_24_out, or_25_out);
  and and_15 (and_15_out, _74138_5_pin15, _74138_5_pin14);
  and and_16 (IRQ, DBG_int_enabled, or_27_out);
  Register #(.Bits(8)) register_1 (.D(DATA), .C(~MWRITE), .en(~_74138_3_pin15), .Q(LED_R0));
  Register #(.Bits(8)) register_2 (.D(DATA), .C(~MWRITE), .en(~_74138_3_pin14), .Q(LED_R1));
  Register #(.Bits(8)) register_3 (.D(DATA), .C(~MWRITE), .en(~_74138_3_pin13), .Q(LED_R2));
  Register #(.Bits(8)) register_4 (.D(DATA), .C(~MWRITE), .en(~_74138_3_pin12), .Q(LED_R3));
  Register #(.Bits(8)) register_5 (.D(DATA), .C(~MWRITE), .en(~_74138_3_pin11), .Q(LED_R4));
  Register #(.Bits(8)) register_6 (.D(DATA), .C(~MWRITE), .en(~_74138_3_pin10), .Q(LED_R5));
  Register #(.Bits(8)) register_7 (.D(DATA), .C(~MWRITE), .en(~_74138_3_pin9), .Q(LED_R6));
  Register #(.Bits(8)) register_8 (.D(DATA), .C(~MWRITE), .en(~_74138_3_pin7), .Q(LED_R7));
  assign DATA = ~_74138_4_pin15 ? IN_0 : 8'bz;  // DriverInvSel driverinvsel_5
  assign DATA = ~_74138_4_pin14 ? IN_1 : 8'bz;  // DriverInvSel driverinvsel_6
  assign DATA = ~_74138_4_pin13 ? IN_2 : 8'bz;  // DriverInvSel driverinvsel_7
  assign DATA = ~_74138_4_pin12 ? IN_3 : 8'bz;  // DriverInvSel driverinvsel_8
  assign DATA = ~_74138_4_pin11 ? IN_4 : 8'bz;  // DriverInvSel driverinvsel_9
  assign DATA = ~_74138_4_pin10 ? IN_5 : 8'bz;  // DriverInvSel driverinvsel_10
  assign DATA = ~_74138_4_pin9 ? IN_6 : 8'bz;  // DriverInvSel driverinvsel_11
  assign DATA = ~_74138_4_pin7 ? {8{1'b0}} : 8'bz;  // DriverInvSel driverinvsel_12

  // Notes on the sheet:
  //   DATA: pin 1
  //   ADDRESS: pin 4
  //   MREAD: pin 2, default 1
  //   MWRITE: pin 3, default 1
  //   LED_R0: pin 34
  //   LED_R1: pin 33
  //   LED_R2: pin 32
  //   LED_R3: pin 31
  //   LED_R4: pin 30
  //   LED_R5: pin 29
  //   LED_R6: pin 28
  //   LED_R7: pin 27
  //   IN_0: pin 26
  //   IN_1: pin 25
  //   IN_2: pin 24
  //   IN_3: pin 23
  //   IN_4: pin 22
  //   IN_5: pin 21
  //   IN_6: pin 20
  //   INT_0_EDGE: pin 7
  //   INT_1_EDGE: pin 8
  //   INT_2_EDGE: pin 9
  //   INT_3_LEVEL: pin 10
  //   P0: pin 6
  //   RST: pin 5
  //   IRQ: pin 11
  //   iv_o: pin 12, default 1
  //   ei: pin 13, default 1
  //   TERM_SEL: pin 14
  //   DBG_int_enabled: pin 15
  //   DBG_TLB_index: pin 16
  //   STORAGE_SEL: pin 19
  //   pg_dis: pin 17, default 1
  //   TLB Index
  //   Reset
  //   Set
  //   Paging Enable
  //   Enabled = high
  //   SEL TLB FLAGS
  //   READ
  //   TLBF
  //   WRITE
  //   TLBF
  //   0x0000-0x3fff
  //   0x4000-0x5fff
  //   0x6000-0x7fff
  //   READ
  //   TLB
  //   SEL TLB
  //   WRITE
  //   TLB
  //   Rom loads rom.hex
  //   Present
  //   RW
  //   0x4000-0x43ff
  //   0x4400-0x47ff
  //   0x4800-0x4bff
  //   0x4800-0x4801
  //   0x4802
  //   0x4803
  //   0x4804
endmodule
