// Digital circuit ata.dig as structural Verilog
module ata (
  input  RST,
  input  WE,
  input  OE,
  input  [7:0] A_mid,
  input  [7:0] A_high,
  input  CS,
  input  [7:0] Data,
  output [7:0] DBG
);

  wire and_1_out, or_1_out;

  and and_1 (and_1_out, WE, OE);
  or or_1 (or_1_out, CS, and_1_out);
  Counter #(.Bits(8)) counter_1 (.en(1'b1), .C(or_1_out), .clr(RST), .out(DBG));  // open: ovf
  EEPROM #(.AddrBits(19), .Bits(8)) Storage (.A({A_high[2:0], A_mid, DBG}), .CS(~CS), .WE(~WE), .OE(~OE), .D(Data));

  // Notes on the sheet:
  //   contents of Storage (hex, n*v repeats v):
  //   66,69,6c,65,32,7*0,2,0,e,0,66,69,6c,65,31,7*0,3,0,3d,0,6e,75,6d
  //   ,73,8*0,4,0,14,9,74,65,73,74,5f,61,70,70,2e,62,69,0,e,0,b0,0,74
  //   ,65,73,74,5f,6d,6b,66,73,2e,63,0,f,0,f6,6,61,70,70,9*0,16,0,b0
  //   ,417*0,74,68,69,73,20,69,73,20,66,69,6c,65,32,a,242*0,54,68,69
  //   ,73,20,69,73,20,66,69,6c,65,20,31,20,6f,6e,20,66,73,a,77,69,74
  //   ,68,20,73,6f,6d,65,20,6c,69,6e,65,73,20,68,65,72,65,a,31,32,33
  //   ,a,34,35,36,37,a,38,39,30,a,2d,65,6e,64,2d,a,195*0,30,31,32,33
  //   ,34,35,36,37,38,39,30,31,32,33,34,35,36,37,38,39,30,31,32,33,34
  //   ,35,36,37,38,39,30,31,32,33,34,35,36,37,38,39,30,31,32,33,34,35
  //   ,36,37,38,39,30,31,32,33,34,35,36,37,38,39,30,31,32,33,34,35,36
  //   ,37,38,39,30,31,32,33,34,35,36,37,38,39,30,31,32,33,34,35,36,37
  //   ,38,39,30,31,32,33,34,35,36,37,38,39,a,30,31,32,33,34,35,36,37
  //   ,38,39,30,31,32,33,34,35,36,37,38,39,30,31,32,33,34,35,36,37,38
  //   ,39,30,31,32,33,34,35,36,37,38,39,30,31,32,33,34,35,36,37,38,39
  //   ,30,31,32,33,34,35,36,37,38,39,30,31,32,33,34,35,36,37,38,39,30
  //   ,31,32,33,34,35,36,37,38,39,30,31,32,33,34,35,36,37,38,39,30,31
  //   ,32,33,34,35,36,37,38,39,a,30,31,32,33,34,35,36,37,38,39,30,31
  //   ,32,33,34,35,36,37,38,39,30,31,32,33,34,35,36,37,38,39,30,31,32
  //   ,33,34,35,36,37,38,39,30,31,32,33,34,35,36,37,38,39,30,31,32,33
  //   ,34,35,36,37,38,39,30,31,32,33,34,35,36,37,38,39,30,31,32,33,34
  //   ,35,36,37,38,39,30,31,32,33,34,35,36,37,38,39,30,31,32,33,34,35
  //   ,36,37,38,39,a,30,31,32,33,34,35,36,37,38,39,30,31,32,33,34,35
  //   ,36,37,38,39,30,31,32,33,34,35,36,37,38,39,30,31,32,33,34,35,36
  //   ,37,38,39,30,31,32,33,34,35,36,37,38,39,30,31,32,33,34,35,36,37
  //   ,38,39,30,31,32,33,34,35,36,37,38,39,30,31,32,33,34,35,36,37,38
  //   ,39,30,31,32,33,34,35,36,37,38,39,30,31,32,33,34,35,36,37,38,39
  //   ,a,30,31,32,33,34,35,36,37,38,39,30,31,32,33,34,35,36,37,38,39
  //   ,30,31,32,33,34,35,36,37,38,39,30,31,32,33,34,35,36,37,38,39,30
  //   ,31,32,33,34,35,36,37,38,39,30,31,32,33,34,35,36,37,38,39,30,31
  //   ,32,33,34,35,36,37,38,39,30,31,32,33,34,35,36,37,38,39,30,31,32
  //   ,33,34,35,36,37,38,39,30,31,32,33,34,35,36,37,38,39,a,30,31,32
  //   ,33,34,35,36,37,38,39,30,31,32,33,34,35,36,37,38,39,30,31,32,33
  //   ,34,35,36,37,38,39,30,31,32,33,34,35,36,37,38,39,30,31,32,33,34
  //   ,35,36,37,38,39,30,31,32,33,34,35,36,37,38,39,30,31,32,33,34,35
  //   ,36,37,38,39,30,31,32,33,34,35,36,37,38,39,30,31,32,33,34,35,36
  //   ,37,38,39,30,31,32,33,34,35,36,37,38,39,a,30,31,32,33,34,35,36
  //   ,37,38,39,30,31,32,33,34,35,36,37,38,39,30,31,32,33,34,35,36,37
  //   ,38,39,30,31,32,33,34,35,36,37,38,39,30,31,32,33,34,35,36,37,38
  //   ,39,30,31,32,33,34,35,36,37,38,39,30,31,32,33,34,35,36,37,38,39
  //   ,30,31,32,33,34,35,36,37,38,39,30,31,32,33,34,35,36,37,38,39,30
  //   ,31,32,33,34,35,36,37,38,39,a,30,31,32,33,34,35,36,37,38,39,30
  //   ,31,32,33,34,35,36,37,38,39,30,31,32,33,34,35,36,37,38,39,30,31
  //   ,32,33,34,35,36,37,38,39,30,31,32,33,34,35,36,37,38,39,30,31,32
  //   ,33,34,35,36,37,38,39,30,31,32,33,34,35,36,37,38,39,30,31,32,33
  //   ,34,35,36,37,38,39,30,31,32,33,34,35,36,37,38,39,30,31,32,33,34
  //   ,35,36,37,38,39,a,30,31,32,33,34,35,36,37,38,39,30,31,32,33,34
  //   ,35,36,37,38,39,30,31,32,33,34,35,36,37,38,39,30,31,32,33,34,35
  //   ,36,37,38,39,30,31,32,33,34,35,36,37,38,39,30,31,32,33,34,35,36
  //   ,37,38,39,30,31,32,33,34,35,36,37,38,39,30,31,32,33,34,35,36,37
  //   ,38,39,30,31,32,33,34,35,36,37,38,39,30,31,32,33,34,35,36,37,38
  //   ,39,a,30,31,32,33,34,35,36,37,38,39,30,31,32,33,34,35,36,37,38
  //   ,39,30,31,32,33,34,35,36,37,38,39,30,31,32,33,34,35,36,37,38,39
  //   ,30,31,32,33,34,35,36,37,38,39,30,31,32,33,34,35,36,37,38,39,30
  //   ,31,32,33,34,35,36,37,38,39,30,31,32,33,34,35,36,37,38,39,30,31
  //   ,32,33,34,35,36,37,38,39,30,31,32,33,34,35,36,37,38,39,a,30,31
  //   ,32,33,34,35,36,37,38,39,30,31,32,33,34,35,36,37,38,39,30,31,32
  //   ,33,34,35,36,37,38,39,30,31,32,33,34,35,36,37,38,39,30,31,32,33
  //   ,34,35,36,37,38,39,30,31,32,33,34,35,36,37,38,39,30,31,32,33,34
  //   ,35,36,37,38,39,30,31,32,33,34,35,36,37,38,39,30,31,32,33,34,35
  //   ,36,37,38,39,30,31,32,33,34,35,36,37,38,39,a,30,31,32,33,34,35
  //   ,36,37,38,39,30,31,32,33,34,35,36,37,38,39,30,31,32,33,34,35,36
  //   ,37,38,39,30,31,32,33,34,35,36,37,38,39,30,31,32,33,34,35,36,37
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endmodule
