// Digital circuit cpu.dig as structural Verilog
module cpu (
  input  clk
);

  wire alu_board_1_c, alu_board_1_of, alu_board_1_sf, alu_board_1_z, and_1_out, and_2_out, decode_1_a_i,
       decode_1_a_o, decode_1_alu_d, decode_1_alu_latch, decode_1_aluf_d, decode_1_b_i, decode_1_b_o,
       decode_1_di_iv_o, decode_1_ei, decode_1_f_i, decode_1_f_o, decode_1_fault, decode_1_mf_a,
       decode_1_mh_i, decode_1_mh_o, decode_1_ml_i, decode_1_ml_o, decode_1_mread, decode_1_mwrite,
       decode_1_off_i, decode_1_off_o, decode_1_pac_a, decode_1_pac_plus__plus, decode_1_pah_i,
       decode_1_pah_o, decode_1_pal_i, decode_1_pal_o, decode_1_pbc_a, decode_1_pbc_plus__plus,
       decode_1_pbh_i, decode_1_pbh_o, decode_1_pbl_i, decode_1_pbl_o, decode_1_s_a, decode_1_s_rst,
       decode_1_sel_high, decode_1_sh_i, decode_1_sh_o, decode_1_sl, decode_1_sl_i, decode_1_sl_o,
       decode_1_sl_plus__plus, delay_1_out, delay_2_out, delay_3_out, mmu_1_dbg_int_enabled, mmu_1_irq,
       mmu_1_storage_sel, mmu_1_term_sel, not_1_out, not_2_out, not_3_out, not_4_out, not_5_out, or_1_out,
       or_2_out, or_3_out, reset_1_out, telnet_1_av;
  wire [3:0] _16_bit_reg_cnt_1_data_out, _16_bit_reg_cnt_1_data_out_2, _16_bit_reg_cnt_2_dbg_2,
       _16_bit_reg_cnt_2_dbg_3, _16_bit_reg_cnt_3_dbg_2, _16_bit_reg_cnt_3_dbg_3, alu_board_1_dbg_a,
       alu_board_1_dbg_a_2, alu_board_1_dbg_b, alu_board_1_dbg_b_2, decode_1_address_2, decode_1_address_3,
       decode_1_dbg, mar_1_dbg_2, mar_1_dbg_3;
  wire [4:0] decode_1_alu_op;
  wire [7:0] _16_bit_reg_cnt_2_dbg, _16_bit_reg_cnt_3_dbg, button_1_out, decode_1_address, dipswitch_1_out,
       dipswitch_3_out, mar_1_dbg, mmu_1_dbg_tlb_index, mmu_1_led_r0, mmu_1_led_r1, mmu_1_led_r2,
       mmu_1_led_r3, mmu_1_led_r4, mmu_1_led_r5, mmu_1_led_r6, mmu_1_led_r7;
  wire [7:4] decode_1_dbg_2;
  wire [15:0] _16_bit_reg_cnt_1_dbg;

  Seven_Seg_Hex seven_seg_hex_1 (.d(decode_1_dbg_2), .dp(1'b0));
  not not_1 (not_1_out, decode_1_fault);
  and and_1 (and_1_out, clk, not_1_out);
  Seven_Seg_Hex seven_seg_hex_2 (.d(decode_1_dbg), .dp(1'b0));
  Seven_Seg_Hex seven_seg_hex_3 (.d(_16_bit_reg_cnt_1_data_out_2), .dp(1'b0));
  Seven_Seg_Hex seven_seg_hex_4 (.d(_16_bit_reg_cnt_1_data_out), .dp(1'b0));
  decode decode_1 (
    .RST(reset_1_out), .DATA({_16_bit_reg_cnt_1_data_out_2, _16_bit_reg_cnt_1_data_out}), .clk(and_1_out),
    .C(alu_board_1_c), .Z(alu_board_1_z), .SF(alu_board_1_sf), .OF(alu_board_1_of), .INT(mmu_1_irq),
    .b_o(decode_1_b_o), .sh_o(decode_1_sh_o), .sl_o(decode_1_sl_o), .mh_o(decode_1_mh_o),
    .ml_o(decode_1_ml_o), .off_o(decode_1_off_o), .s_a(decode_1_s_a), .alu_d(decode_1_alu_d),
    .mf_a(decode_1_mf_a), .aluf_d(decode_1_aluf_d), .f_o(decode_1_f_o), .b_i(decode_1_b_i),
    .sh_i(decode_1_sh_i), .sl_i(decode_1_sl_i), .mh_i(decode_1_mh_i), .ml_i(decode_1_ml_i),
    .off_i(decode_1_off_i), .sl(decode_1_sl), .sl_plus__plus(decode_1_sl_plus__plus), .f_i(decode_1_f_i),
    .A_i(decode_1_a_i), .A_o(decode_1_a_o), .MREAD(decode_1_mread), .MWRITE(decode_1_mwrite),
    .pAh_o(decode_1_pah_o), .pAl_o(decode_1_pal_o), .pAh_i(decode_1_pah_i), .pAl_i(decode_1_pal_i),
    .pBc_plus__plus(decode_1_pbc_plus__plus), .pBc_a(decode_1_pbc_a), .pBh_o(decode_1_pbh_o),
    .pBl_o(decode_1_pbl_o), .pBh_i(decode_1_pbh_i), .pBl_i(decode_1_pbl_i),
    .pAc_plus__plus(decode_1_pac_plus__plus), .pAc_a(decode_1_pac_a),
    .Address({decode_1_address_3, decode_1_address_2, decode_1_address}), .ALU_op(decode_1_alu_op),
    .ALU_latch(decode_1_alu_latch), .ei(decode_1_ei), .s_rst(decode_1_s_rst), .di_iv_o(decode_1_di_iv_o),
    .DBG({decode_1_dbg_2, decode_1_dbg}), .FAULT(decode_1_fault), .sel_high(decode_1_sel_high));  // open: NC, NC1, NC2
  Seven_Seg_Hex seven_seg_hex_5 (.d(decode_1_address_3), .dp(1'b0));
  Seven_Seg_Hex seven_seg_hex_6 (.d(decode_1_address_2), .dp(1'b0));
  Seven_Seg_Hex seven_seg_hex_7 (.d(decode_1_address[7:4]), .dp(1'b0));
  Seven_Seg_Hex seven_seg_hex_8 (.d(decode_1_address[3:0]), .dp(1'b0));
  _16_bit_reg_cnt _16_bit_reg_cnt_1 (
    .LOW_D(decode_1_sl_o), .HIGH_D(decode_1_sh_o), .OUT_A(decode_1_s_a), .LOW_LD(decode_1_sl_i),
    .HIGH_LD(decode_1_sh_i), .INC(decode_1_sl_plus__plus), .DEC(decode_1_sl), .RST(decode_1_s_rst),
    .DATA({_16_bit_reg_cnt_1_data_out_2, _16_bit_reg_cnt_1_data_out}),
    .DATA_OUT({_16_bit_reg_cnt_1_data_out_2, _16_bit_reg_cnt_1_data_out}),
    .Address({decode_1_address_3, decode_1_address_2, decode_1_address}), .DBG(_16_bit_reg_cnt_1_dbg));
  alu_board alu_board_1 (
    .DATA({_16_bit_reg_cnt_1_data_out_2, _16_bit_reg_cnt_1_data_out}), .A_i(decode_1_a_i),
    .A_o(decode_1_a_o), .ALU_latch(decode_1_alu_latch), .B_i(decode_1_b_i), .B_o(decode_1_b_o),
    .ALU_OP(decode_1_alu_op), .ALU_d(decode_1_alu_d), .ALUF_d(decode_1_aluf_d), .F_o(decode_1_f_o),
    .F_i(decode_1_f_i), .DATA_OUT({_16_bit_reg_cnt_1_data_out_2, _16_bit_reg_cnt_1_data_out}),
    .C(alu_board_1_c), .Z(alu_board_1_z), .SF(alu_board_1_sf), .OF(alu_board_1_of),
    .DBG_A({alu_board_1_dbg_a_2, alu_board_1_dbg_a}), .DBG_B({alu_board_1_dbg_b_2, alu_board_1_dbg_b}));
  mar mar_1 (
    .LOW_D(decode_1_ml_o), .HIGH_D(decode_1_mh_o), .MF_A(decode_1_mf_a), .LOW_LD(decode_1_ml_i),
    .HIGH_LD(decode_1_mh_i), .INC(1'b1), .DEC(1'b1), .RST(reset_1_out),
    .DATA({_16_bit_reg_cnt_1_data_out_2, _16_bit_reg_cnt_1_data_out}), .OFF_i(decode_1_off_i),
    .OFF_o(decode_1_off_o), .sel_high(decode_1_sel_high), .imm(decode_1_alu_op),
    .DATA_OUT({_16_bit_reg_cnt_1_data_out_2, _16_bit_reg_cnt_1_data_out}),
    .Address({decode_1_address_3, decode_1_address_2, decode_1_address}),
    .DBG({mar_1_dbg_3, mar_1_dbg_2, mar_1_dbg}));
  _16_bit_reg_cnt _16_bit_reg_cnt_2 (
    .LOW_D(decode_1_pal_o), .HIGH_D(decode_1_pah_o), .OUT_A(decode_1_pac_a), .LOW_LD(decode_1_pal_i),
    .HIGH_LD(decode_1_pah_i), .INC(decode_1_pac_plus__plus), .DEC(1'b1), .RST(reset_1_out),
    .DATA({_16_bit_reg_cnt_1_data_out_2, _16_bit_reg_cnt_1_data_out}),
    .DATA_OUT({_16_bit_reg_cnt_1_data_out_2, _16_bit_reg_cnt_1_data_out}),
    .Address({decode_1_address_3, decode_1_address_2, decode_1_address}),
    .DBG({_16_bit_reg_cnt_2_dbg_3, _16_bit_reg_cnt_2_dbg_2, _16_bit_reg_cnt_2_dbg}));
  _16_bit_reg_cnt _16_bit_reg_cnt_3 (
    .LOW_D(decode_1_pbl_o), .HIGH_D(decode_1_pbh_o), .OUT_A(decode_1_pbc_a), .LOW_LD(decode_1_pbl_i),
    .HIGH_LD(decode_1_pbh_i), .INC(decode_1_pbc_plus__plus), .DEC(1'b1), .RST(reset_1_out),
    .DATA({_16_bit_reg_cnt_1_data_out_2, _16_bit_reg_cnt_1_data_out}),
    .DATA_OUT({_16_bit_reg_cnt_1_data_out_2, _16_bit_reg_cnt_1_data_out}),
    .Address({decode_1_address_3, decode_1_address_2, decode_1_address}),
    .DBG({_16_bit_reg_cnt_3_dbg_3, _16_bit_reg_cnt_3_dbg_2, _16_bit_reg_cnt_3_dbg}));
  Reset #(.invertOutput("false")) reset_1 (.out(reset_1_out));
  Seven_Seg_Hex seven_seg_hex_9 (.d(alu_board_1_dbg_a_2), .dp(1'b0));
  Seven_Seg_Hex seven_seg_hex_10 (.d(mar_1_dbg_3), .dp(1'b0));
  Seven_Seg_Hex seven_seg_hex_11 (.d(_16_bit_reg_cnt_2_dbg_3), .dp(1'b0));
  Seven_Seg_Hex seven_seg_hex_12 (.d(_16_bit_reg_cnt_3_dbg_3), .dp(1'b0));
  LED led_1 (.in(mmu_1_dbg_int_enabled));
  Seven_Seg_Hex seven_seg_hex_13 (.d(alu_board_1_dbg_a), .dp(1'b0));
  Seven_Seg_Hex seven_seg_hex_14 (.d(mar_1_dbg_2), .dp(1'b0));
  Seven_Seg_Hex seven_seg_hex_15 (.d(_16_bit_reg_cnt_2_dbg_2), .dp(1'b0));
  Seven_Seg_Hex seven_seg_hex_16 (.d(_16_bit_reg_cnt_3_dbg_2), .dp(1'b0));
  MMU mmu_1 (
    .DATA({_16_bit_reg_cnt_1_data_out_2, _16_bit_reg_cnt_1_data_out}),
    .ADDRESS({decode_1_address_3, decode_1_address_2, decode_1_address}), .MREAD(decode_1_mread),
    .MWRITE(decode_1_mwrite), .LED_R0(mmu_1_led_r0), .LED_R1(mmu_1_led_r1), .LED_R2(mmu_1_led_r2),
    .LED_R3(mmu_1_led_r3), .LED_R4(mmu_1_led_r4), .LED_R5(mmu_1_led_r5), .LED_R6(mmu_1_led_r6),
    .LED_R7(mmu_1_led_r7), .IN_0(button_1_out), .IN_1(dipswitch_1_out), .IN_2(dipswitch_3_out),
    .IN_3({8{1'b0}}), .IN_4({8{1'b0}}), .IN_5({8{1'b0}}), .IN_6({8{1'b0}}), .INT_0_EDGE(and_2_out),
    .INT_1_EDGE(button_1_out[1]), .INT_2_EDGE(button_1_out[2]), .INT_3_LEVEL(telnet_1_av),
    .P0(decode_1_alu_latch), .RST(reset_1_out), .IRQ(mmu_1_irq), .iv_o(decode_1_di_iv_o), .ei(decode_1_ei),
    .TERM_SEL(mmu_1_term_sel), .DBG_int_enabled(mmu_1_dbg_int_enabled), .DBG_TLB_index(mmu_1_dbg_tlb_index),
    .STORAGE_SEL(mmu_1_storage_sel));  // open: pg_dis
  or or_1 (or_1_out, mmu_1_term_sel, decode_1_mwrite);
  or or_2 (or_2_out, mmu_1_term_sel, decode_1_mread);
  Seven_Seg_Hex seven_seg_hex_17 (.d(alu_board_1_dbg_b_2), .dp(1'b0));
  Seven_Seg_Hex seven_seg_hex_18 (.d(mar_1_dbg[7:4]), .dp(1'b0));
  Seven_Seg_Hex seven_seg_hex_19 (.d(_16_bit_reg_cnt_2_dbg[7:4]), .dp(1'b0));
  Seven_Seg_Hex seven_seg_hex_20 (.d(_16_bit_reg_cnt_3_dbg[7:4]), .dp(1'b0));
  Seven_Seg_Hex seven_seg_hex_21 (.d(alu_board_1_dbg_b), .dp(1'b0));
  Seven_Seg_Hex seven_seg_hex_22 (.d(mar_1_dbg[3:0]), .dp(1'b0));
  Seven_Seg_Hex seven_seg_hex_23 (.d(_16_bit_reg_cnt_2_dbg[3:0]), .dp(1'b0));
  Seven_Seg_Hex seven_seg_hex_24 (.d(_16_bit_reg_cnt_3_dbg[3:0]), .dp(1'b0));
  Seven_Seg_Hex seven_seg_hex_25 (.d(mmu_1_dbg_tlb_index[7:4]), .dp(1'b0));
  not not_2 (not_2_out, or_1_out);
  not not_3 (not_3_out, or_2_out);
  Seven_Seg_Hex seven_seg_hex_26 (.d(mmu_1_dbg_tlb_index[3:0]), .dp(1'b0));
  Seven_Seg_Hex seven_seg_hex_27 (.d(_16_bit_reg_cnt_1_dbg[15:12]), .dp(1'b0));
  or or_3 (or_3_out, not_2_out, not_3_out);
  Seven_Seg_Hex seven_seg_hex_28 (.d(_16_bit_reg_cnt_1_dbg[11:8]), .dp(1'b0));
  Seven_Seg_Hex seven_seg_hex_29 (.d(_16_bit_reg_cnt_1_dbg[7:4]), .dp(1'b0));
  not not_4 (not_4_out, or_3_out);
  Button button_1 (.out(button_1_out[7]));
  Button button_2 (.out(button_1_out[6]));
  DipSwitch dipswitch_1 (.out(dipswitch_1_out[7]));
  DipSwitch dipswitch_2 (.out(dipswitch_1_out[6]));
  DipSwitch dipswitch_3 (.out(dipswitch_3_out[7]));
  DipSwitch dipswitch_4 (.out(dipswitch_3_out[6]));
  Seven_Seg_Hex seven_seg_hex_30 (.d(_16_bit_reg_cnt_1_dbg[3:0]), .dp(1'b0));
  Delay #(.delayTime(5)) delay_1 (.in(not_2_out), .out(delay_1_out));
  Delay #(.delayTime(5)) delay_2 (.in(not_3_out), .out(delay_2_out));
  LightBulb lightbulb_1 (.A(1'b0), .B(mmu_1_led_r0[7]));
  LightBulb lightbulb_2 (.A(1'b0), .B(mmu_1_led_r1[7]));
  LightBulb lightbulb_3 (.A(1'b0), .B(mmu_1_led_r2[7]));
  LightBulb lightbulb_4 (.A(1'b0), .B(mmu_1_led_r3[7]));
  LightBulb lightbulb_5 (.A(1'b0), .B(mmu_1_led_r4[7]));
  LightBulb lightbulb_6 (.A(1'b0), .B(mmu_1_led_r5[7]));
  LightBulb lightbulb_7 (.A(1'b0), .B(mmu_1_led_r6[7]));
  LightBulb lightbulb_8 (.A(1'b0), .B(mmu_1_led_r7[7]));
  Button button_3 (.out(button_1_out[5]));
  Button button_4 (.out(button_1_out[4]));
  DipSwitch dipswitch_5 (.out(dipswitch_1_out[5]));
  DipSwitch dipswitch_6 (.out(dipswitch_1_out[4]));
  DipSwitch dipswitch_7 (.out(dipswitch_3_out[5]));
  DipSwitch dipswitch_8 (.out(dipswitch_3_out[4]));
  LightBulb lightbulb_9 (.A(1'b0), .B(mmu_1_led_r0[6]));
  LightBulb lightbulb_10 (.A(1'b0), .B(mmu_1_led_r0[5]));
  LightBulb lightbulb_11 (.A(1'b0), .B(mmu_1_led_r1[6]));
  LightBulb lightbulb_12 (.A(1'b0), .B(mmu_1_led_r1[5]));
  LightBulb lightbulb_13 (.A(1'b0), .B(mmu_1_led_r2[6]));
  LightBulb lightbulb_14 (.A(1'b0), .B(mmu_1_led_r2[5]));
  LightBulb lightbulb_15 (.A(1'b0), .B(mmu_1_led_r3[6]));
  LightBulb lightbulb_16 (.A(1'b0), .B(mmu_1_led_r3[5]));
  LightBulb lightbulb_17 (.A(1'b0), .B(mmu_1_led_r4[6]));
  LightBulb lightbulb_18 (.A(1'b0), .B(mmu_1_led_r4[5]));
  LightBulb lightbulb_19 (.A(1'b0), .B(mmu_1_led_r5[6]));
  LightBulb lightbulb_20 (.A(1'b0), .B(mmu_1_led_r5[5]));
  LightBulb lightbulb_21 (.A(1'b0), .B(mmu_1_led_r6[6]));
  LightBulb lightbulb_22 (.A(1'b0), .B(mmu_1_led_r6[5]));
  LightBulb lightbulb_23 (.A(1'b0), .B(mmu_1_led_r7[6]));
  LightBulb lightbulb_24 (.A(1'b0), .B(mmu_1_led_r7[5]));
  Button button_5 (.out(button_1_out[3]));
  Button button_6 (.out(button_1_out[2]));
  DipSwitch dipswitch_9 (.out(dipswitch_1_out[3]));
  DipSwitch dipswitch_10 (.out(dipswitch_1_out[2]));
  DipSwitch dipswitch_11 (.out(dipswitch_3_out[3]));
  DipSwitch dipswitch_12 (.out(dipswitch_3_out[2]));
  LightBulb lightbulb_25 (.A(1'b0), .B(mmu_1_led_r0[4]));
  LightBulb lightbulb_26 (.A(1'b0), .B(mmu_1_led_r0[3]));
  LightBulb lightbulb_27 (.A(1'b0), .B(mmu_1_led_r1[4]));
  LightBulb lightbulb_28 (.A(1'b0), .B(mmu_1_led_r1[3]));
  LightBulb lightbulb_29 (.A(1'b0), .B(mmu_1_led_r2[4]));
  LightBulb lightbulb_30 (.A(1'b0), .B(mmu_1_led_r2[3]));
  LightBulb lightbulb_31 (.A(1'b0), .B(mmu_1_led_r3[4]));
  LightBulb lightbulb_32 (.A(1'b0), .B(mmu_1_led_r3[3]));
  LightBulb lightbulb_33 (.A(1'b0), .B(mmu_1_led_r4[4]));
  LightBulb lightbulb_34 (.A(1'b0), .B(mmu_1_led_r4[3]));
  LightBulb lightbulb_35 (.A(1'b0), .B(mmu_1_led_r5[4]));
  LightBulb lightbulb_36 (.A(1'b0), .B(mmu_1_led_r5[3]));
  LightBulb lightbulb_37 (.A(1'b0), .B(mmu_1_led_r6[4]));
  LightBulb lightbulb_38 (.A(1'b0), .B(mmu_1_led_r6[3]));
  LightBulb lightbulb_39 (.A(1'b0), .B(mmu_1_led_r7[4]));
  LightBulb lightbulb_40 (.A(1'b0), .B(mmu_1_led_r7[3]));
  Button button_7 (.out(button_1_out[1]));
  Button UP (.out(button_1_out[0]));
  DipSwitch dipswitch_13 (.out(dipswitch_1_out[1]));
  DipSwitch dipswitch_14 (.out(dipswitch_1_out[0]));
  DipSwitch dipswitch_15 (.out(dipswitch_3_out[1]));
  DipSwitch dipswitch_16 (.out(dipswitch_3_out[0]));
  Telnet #(.telnetEscape("false"), .port(1234)) telnet_1 (
    .in({_16_bit_reg_cnt_1_data_out_2, _16_bit_reg_cnt_1_data_out}), .C(not_4_out), .wr(delay_1_out),
    .rd(delay_2_out), .out({_16_bit_reg_cnt_1_data_out_2, _16_bit_reg_cnt_1_data_out}), .av(telnet_1_av));
  LightBulb lightbulb_41 (.A(1'b0), .B(mmu_1_led_r0[2]));
  LightBulb lightbulb_42 (.A(1'b0), .B(mmu_1_led_r0[1]));
  LightBulb lightbulb_43 (.A(1'b0), .B(mmu_1_led_r1[2]));
  LightBulb lightbulb_44 (.A(1'b0), .B(mmu_1_led_r1[1]));
  LightBulb lightbulb_45 (.A(1'b0), .B(mmu_1_led_r2[2]));
  LightBulb lightbulb_46 (.A(1'b0), .B(mmu_1_led_r2[1]));
  LightBulb lightbulb_47 (.A(1'b0), .B(mmu_1_led_r3[2]));
  LightBulb lightbulb_48 (.A(1'b0), .B(mmu_1_led_r3[1]));
  LightBulb lightbulb_49 (.A(1'b0), .B(mmu_1_led_r4[2]));
  LightBulb lightbulb_50 (.A(1'b0), .B(mmu_1_led_r4[1]));
  LightBulb lightbulb_51 (.A(1'b0), .B(mmu_1_led_r5[2]));
  LightBulb lightbulb_52 (.A(1'b0), .B(mmu_1_led_r5[1]));
  LightBulb lightbulb_53 (.A(1'b0), .B(mmu_1_led_r6[2]));
  LightBulb lightbulb_54 (.A(1'b0), .B(mmu_1_led_r6[1]));
  LightBulb lightbulb_55 (.A(1'b0), .B(mmu_1_led_r7[2]));
  LightBulb lightbulb_56 (.A(1'b0), .B(mmu_1_led_r7[1]));
  LightBulb lightbulb_57 (.A(1'b0), .B(mmu_1_led_r0[0]));
  LightBulb lightbulb_58 (.A(1'b0), .B(mmu_1_led_r1[0]));
  LightBulb lightbulb_59 (.A(1'b0), .B(mmu_1_led_r2[0]));
  LightBulb lightbulb_60 (.A(1'b0), .B(mmu_1_led_r3[0]));
  LightBulb lightbulb_61 (.A(1'b0), .B(mmu_1_led_r4[0]));
  LightBulb lightbulb_62 (.A(1'b0), .B(mmu_1_led_r5[0]));
  LightBulb lightbulb_63 (.A(1'b0), .B(mmu_1_led_r6[0]));
  LightBulb lightbulb_64 (.A(1'b0), .B(mmu_1_led_r7[0]));
  not not_5 (not_5_out, button_1_out[0]);
  Delay delay_3 (.in(not_5_out), .out(delay_3_out));
  and and_2 (and_2_out, button_1_out[0], delay_3_out);
  EEPROM #(.AddrBits(19), .Bits(8)) Storage (
    .A({mmu_1_led_r2[2:0], mmu_1_led_r1, mmu_1_led_r0}), .CS(~mmu_1_storage_sel), .WE(~decode_1_mwrite),
    .OE(~decode_1_mread), .D({_16_bit_reg_cnt_1_data_out_2, _16_bit_reg_cnt_1_data_out}));

  // Notes on the sheet:
  //   clk: Hz: 2147483647
  //   SP
  //   ALU
  //   MAR
  //   PC_a
  //   PC_b
  //   A
  //   BP
  //   PCa
  //   PCb
  //   B
  //   TLB Index
  //   contents of Storage (hex, n*v repeats v):
  //   66,69,6c,65,31,7*0,2,0,3d,0,6e,75,6d,73,8*0,3,0,14,9,74,65,73
  //   ,74,5f,61,73,6d,2e,63,0,0,d,0,d9,38,74,65,73,74,5f,6d,6b,66,73
  //   ,2e,63,0,46,0,f6,6,448*0,54,68,69,73,20,69,73,20,66,69,6c,65,20
  //   ,31,20,6f,6e,20,66,73,a,77,69,74,68,20,73,6f,6d,65,20,6c,69,6e
  //   ,65,73,20,68,65,72,65,a,31,32,33,a,34,35,36,37,a,38,39,30,a,2d
  //   ,65,6e,64,2d,a,195*0,30,31,32,33,34,35,36,37,38,39,30,31,32,33
  //   ,34,35,36,37,38,39,30,31,32,33,34,35,36,37,38,39,30,31,32,33,34
  //   ,35,36,37,38,39,30,31,32,33,34,35,36,37,38,39,30,31,32,33,34,35
  //   ,36,37,38,39,30,31,32,33,34,35,36,37,38,39,30,31,32,33,34,35,36
  //   ,37,38,39,30,31,32,33,34,35,36,37,38,39,30,31,32,33,34,35,36,37
  //   ,38,39,a,30,31,32,33,34,35,36,37,38,39,30,31,32,33,34,35,36,37
  //   ,38,39,30,31,32,33,34,35,36,37,38,39,30,31,32,33,34,35,36,37,38
  //   ,39,30,31,32,33,34,35,36,37,38,39,30,31,32,33,34,35,36,37,38,39
  //   ,30,31,32,33,34,35,36,37,38,39,30,31,32,33,34,35,36,37,38,39,30
  //   ,31,32,33,34,35,36,37,38,39,30,31,32,33,34,35,36,37,38,39,a,30
  //   ,31,32,33,34,35,36,37,38,39,30,31,32,33,34,35,36,37,38,39,30,31
  //   ,32,33,34,35,36,37,38,39,30,31,32,33,34,35,36,37,38,39,30,31,32
  //   ,33,34,35,36,37,38,39,30,31,32,33,34,35,36,37,38,39,30,31,32,33
  //   ,34,35,36,37,38,39,30,31,32,33,34,35,36,37,38,39,30,31,32,33,34
  //   ,35,36,37,38,39,30,31,32,33,34,35,36,37,38,39,a,30,31,32,33,34
  //   ,35,36,37,38,39,30,31,32,33,34,35,36,37,38,39,30,31,32,33,34,35
  //   ,36,37,38,39,30,31,32,33,34,35,36,37,38,39,30,31,32,33,34,35,36
  //   ,37,38,39,30,31,32,33,34,35,36,37,38,39,30,31,32,33,34,35,36,37
  //   ,38,39,30,31,32,33,34,35,36,37,38,39,30,31,32,33,34,35,36,37,38
  //   ,39,30,31,32,33,34,35,36,37,38,39,a,30,31,32,33,34,35,36,37,38
  //   ,39,30,31,32,33,34,35,36,37,38,39,30,31,32,33,34,35,36,37,38,39
  //   ,30,31,32,33,34,35,36,37,38,39,30,31,32,33,34,35,36,37,38,39,30
  //   ,31,32,33,34,35,36,37,38,39,30,31,32,33,34,35,36,37,38,39,30,31
  //   ,32,33,34,35,36,37,38,39,30,31,32,33,34,35,36,37,38,39,30,31,32
  //   ,33,34,35,36,37,38,39,a,30,31,32,33,34,35,36,37,38,39,30,31,32
  //   ,33,34,35,36,37,38,39,30,31,32,33,34,35,36,37,38,39,30,31,32,33
  //   ,34,35,36,37,38,39,30,31,32,33,34,35,36,37,38,39,30,31,32,33,34
  //   ,35,36,37,38,39,30,31,32,33,34,35,36,37,38,39,30,31,32,33,34,35
  //   ,36,37,38,39,30,31,32,33,34,35,36,37,38,39,30,31,32,33,34,35,36
  //   ,37,38,39,a,30,31,32,33,34,35,36,37,38,39,30,31,32,33,34,35,36
  //   ,37,38,39,30,31,32,33,34,35,36,37,38,39,30,31,32,33,34,35,36,37
  //   ,38,39,30,31,32,33,34,35,36,37,38,39,30,31,32,33,34,35,36,37,38
  //   ,39,30,31,32,33,34,35,36,37,38,39,30,31,32,33,34,35,36,37,38,39
  //   ,30,31,32,33,34,35,36,37,38,39,30,31,32,33,34,35,36,37,38,39,a
  //   ,30,31,32,33,34,35,36,37,38,39,30,31,32,33,34,35,36,37,38,39,30
  //   ,31,32,33,34,35,36,37,38,39,30,31,32,33,34,35,36,37,38,39,30,31
  //   ,32,33,34,35,36,37,38,39,30,31,32,33,34,35,36,37,38,39,30,31,32
  //   ,33,34,35,36,37,38,39,30,31,32,33,34,35,36,37,38,39,30,31,32,33
  //   ,34,35,36,37,38,39,30,31,32,33,34,35,36,37,38,39,a,30,31,32,33
  //   ,34,35,36,37,38,39,30,31,32,33,34,35,36,37,38,39,30,31,32,33,34
  //   ,35,36,37,38,39,30,31,32,33,34,35,36,37,38,39,30,31,32,33,34,35
  //   ,36,37,38,39,30,31,32,33,34,35,36,37,38,39,30,31,32,33,34,35,36
  //   ,37,38,39,30,31,32,33,34,35,36,37,38,39,30,31,32,33,34,35,36,37
  //   ,38,39,30,31,32,33,34,35,36,37,38,39,a,30,31,32,33,34,35,36,37
  //   ,38,39,30,31,32,33,34,35,36,37,38,39,30,31,32,33,34,35,36,37,38
  //   ,39,30,31,32,33,34,35,36,37,38,39,30,31,32,33,34,35,36,37,38,39
  //   ,30,31,32,33,34,35,36,37,38,39,30,31,32,33,34,35,36,37,38,39,30
  //   ,31,32,33,34,35,36,37,38,39,30,31,32,33,34,35,36,37,38,39,30,31
  //   ,32,33,34,35,36,37,38,39,a,30,31,32,33,34,35,36,37,38,39,30,31
  //   ,32,33,34,35,36,37,38,39,30,31,32,33,34,35,36,37,38,39,30,31,32
  //   ,33,34,35,36,37,38,39,30,31,32,33,34,35,36,37,38,39,30,31,32,33
  //   ,34,35,36,37,38,39,30,31,32,33,34,35,36,37,38,39,30,31,32,33,34
  //   ,35,36,37,38,39,30,31,32,33,34,35,36,37,38,39,30,31,32,33,34,35
  //   ,36,37,38,39,a,30,31,32,33,34,35,36,37,38,39,30,31,32,33,34,35
  //   ,36,37,38,39,30,31,32,33,34,35,36,37,38,39,30,31,32,33,34,35,36
  //   ,37,38,39,30,31,32,33,34,35,36,37,38,39,30,31,32,33,34,35,36,37
  //   ,38,39,30,31,32,33,34,35,36,37,38,39,30,31,32,33,34,35,36,37,38
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endmodule
