// Logisim project cpu5.circ as structural Verilog: 1 circuit, main circuit main
// ld_flags
module main (
  input  in_1,
  input  in_2,
  input  in_3,
  input  in_4,
  input  in_5,
  input  in_6,
  input  in_7,
  input  in_8,
  input  in_9,
  input  in_10,
  input  in_11
);

  wire a_in, a_out, alu_d, alu_out, and_1_out, and_2_out, and_5_out, and_7_out, and_8_out, and_9_out,
       and_10_out, and_12_out, and_15_out, and_21_out, and_22_out, and_27_out, and_37_out, and_38_out,
       and_45_out, and_46_out, and_47_out, and_51_out, and_52_out, and_53_out, and_54_out, aop_in, b_in,
       b_out, bit_dbl, button_1_out, button_6_out, button_7_out, button_8_out, clock_1_out, cond_true, dec_s,
       decoder_1_out0, decoder_1_out1, decoder_1_out2, decoder_1_out3, decoder_1_out4, decoder_1_out5,
       decoder_1_out6, decoder_1_out7, decoder_2_out0, decoder_4_out13, decoder_5_out1, decoder_5_out2,
       decoder_5_out3, decoder_5_out4, decoder_5_out7, decoder_6_out11, decoder_7_out1, decoder_7_out2,
       decoder_7_out3, decoder_7_out5, decoder_7_out6, decoder_7_out7, dlit_out, dstk_out, flags_in, halt,
       inc_s, inc_x, inc_x0, inc_x1, inc_y, inc_y0, inc_y1, INT_0, INT_1, INT_2, ld_alu_cmd, ld_ir, ld_mh,
       ld_ml, ld_off, ld_sh, ld_sl, ld_xh, ld_xl, ld_yh, ld_yl, ld_zh, ld_zl, lit_out, m_a, m_a0, m_a1,
       mem_in, mem_out, mh_in, ml_in, mr, mr0, mr3, mr4, mw, NO_INT, not_2_out, not_3_out, not_4_out,
       not_5_out, not_7_out, not_8_out, not_9_out, not_10_out, not_11_out, not_13_out, nsel_a_x, off_in,
       or_1_out, or_2_out, or_3_out, or_4_out, or_5_out, or_6_out, or_7_out, or_8_out, or_10_out, or_11_out,
       or_17_out, or_19_out, or_23_out, or_24_out, or_25_out, or_26_out, or_27_out, or_28_out, or_29_out,
       or_31_out, or_33_out, or_34_out, or_35_out, or_36_out, or_37_out, or_38_out, or_39_out, or_40_out, p0,
       s_a, s_a1, sel_a_x, sel_in, sel_out, sel_ram, sh_in, Single_Pulse_q, SL_carry, sl_in, stk_in, stk_out,
       toggle0, toggle1, toggle_reg, toggle_reg_cond, undriven, word2, x_a, x_a0, x_a1, xh_d, XL_carry, xl_d,
       y_a, y_a0, y_a1, yh_d, YL_carry, yl_d, z_a, z_a1, zh_in, zl_in, zm_in, zm_out;
  wire [0:0] IR_q;
  wire [1:0] YH_2_q;
  wire [2:0] and_20_out, IntPend0_q;
  wire [2:2] d_ff_1_q;
  wire [3:0] ALU_Latch_q, ALU_Latch_q_2, B_XH_out, B_XH_out_2, counter_1_q, sel_dst, sel_src;
  wire [7:0] A_XL_out, controlled_buffer_14_out, controlled_buffer_15_out, controlled_buffer_19_out, d_bus,
       FLAG_Latch_q, FLAGS_q, IntEn_q, MH_q, ML_q, OFF_q, R_out, register_1_q, register_2_q, register_3_q,
       register_4_q, register_5_q, register_6_q, register_7_q, register_8_q, register_9_q, rom_1_data,
       rom_2_data, SH_q, SL_q, XH_q, XL_q, YH_q, YL_q, ZH_q, ZL_q;
  wire [15:0] a_bus, adder_1_out;

  Hex_Digit_Display hex_digit_display_1 (.value(d_bus[7:4]));  // open: dp
  Hex_Digit_Display hex_digit_display_2 (.value(d_bus[3:0]));  // open: dp
  not not_1 (sel_ram, a_bus[15]);
  assign d_bus = xl_d ? XL_q : 8'bz;  // Controlled_Buffer controlled_buffer_1
  assign d_bus = xh_d ? XH_q : 8'bz;  // Controlled_Buffer controlled_buffer_2
  assign d_bus = yl_d ? YL_q : 8'bz;  // Controlled_Buffer controlled_buffer_3
  assign d_bus = yh_d ? YH_q : 8'bz;  // Controlled_Buffer controlled_buffer_4
  Register ZL (.D(d_bus), .Q(ZL_q), .clk(ld_zl));  // open: en, clr
  Register OFF (.D(d_bus), .Q(OFF_q), .clk(ld_off));  // open: en, clr
  Register ML (.D(d_bus), .Q(ML_q), .clk(ld_ml));  // open: en, clr
  Register MH (.D(d_bus), .Q(MH_q), .clk(ld_mh));  // open: en, clr
  assign d_bus = in_3 ? SL_q : 8'bz;  // Controlled_Buffer controlled_buffer_5
  assign d_bus = in_4 ? SH_q : 8'bz;  // Controlled_Buffer controlled_buffer_6
  not not_2 (not_2_out, a_bus[14]);
  Counter XL (.load(ld_xl), .D(d_bus), .count(inc_x), .Q(XL_q), .carry(XL_carry), .clk(or_1_out), .clr(button_1_out));
  or or_1 (or_1_out, ld_xl, inc_x);
  and and_1 (and_1_out, inc_x, XL_carry);
  Counter XH (.load(ld_xh), .D(d_bus), .count(and_1_out), .Q(XH_q), .clk(or_2_out), .clr(button_1_out));  // open: carry
  or or_2 (or_2_out, inc_x, ld_xh);
  Counter YL (.load(ld_yl), .D(d_bus), .count(inc_y), .Q(YL_q), .carry(YL_carry), .clk(or_3_out), .clr(button_1_out));
  or or_3 (or_3_out, ld_yl, inc_y);
  and and_2 (and_2_out, inc_y, YL_carry);
  Counter YH (.load(ld_yh), .D(d_bus), .count(and_2_out), .Q(YH_q), .clk(or_4_out), .clr(button_1_out));  // open: carry
  or or_4 (or_4_out, inc_y, ld_yh);
  Register ZH (.D(d_bus), .Q(ZH_q), .clk(ld_zh));  // open: en, clr
  or or_5 (or_5_out, inc_s, dec_s);
  or or_6 (or_6_out, ld_sl, dec_s);
  or or_7 (or_7_out, ld_sl, or_5_out);
  or or_8 (or_8_out, or_5_out, ld_sh);
  Register IR (.D(d_bus), .Q({sel_src, sel_dst[3:1], IR_q[0]}), .clk(ld_ir));  // open: en, clr
  and and_3 (sel_in, not_2_out, a_bus[15]);
  and and_4 (sel_out, a_bus[14], a_bus[15]);
  Hex_Digit_Display hex_digit_display_3 (.value(a_bus[15:12]));  // open: dp
  Button button_1 (.out(button_1_out));
  assign d_bus = in_7 ? ZH_q : 8'bz;  // Controlled_Buffer controlled_buffer_7
  assign d_bus = in_6 ? ZL_q : 8'bz;  // Controlled_Buffer controlled_buffer_8
  assign d_bus = in_8 ? ML_q : 8'bz;  // Controlled_Buffer controlled_buffer_9
  assign a_bus = m_a ? {MH_q, ML_q} : 16'bz;  // Controlled_Buffer MA
  Counter SL (.load(or_6_out), .D(d_bus), .count(or_5_out), .Q(SL_q), .carry(SL_carry), .clk(or_7_out));  // open: clr
  Counter SH (.load(ld_sh), .D(d_bus), .count(SL_carry), .Q(SH_q), .clk(or_8_out));  // open: carry, clr
  and and_5 (and_5_out, sel_out, mw);
  Hex_Digit_Display hex_digit_display_4 (.value(a_bus[7:4]));  // open: dp
  Hex_Digit_Display hex_digit_display_5 (.value(a_bus[11:8]));  // open: dp
  assign a_bus = x_a ? {XH_q, XL_q} : 16'bz;  // Controlled_Buffer XA
  assign a_bus = y_a ? {YH_q, YL_q} : 16'bz;  // Controlled_Buffer YA
  assign a_bus = z_a ? adder_1_out : 16'bz;  // Controlled_Buffer controlled_buffer_10
  Adder #(.width(16)) adder_1 (
    .a({ZH_q, ZL_q}), .b({{9{OFF_q[7]}}, OFF_q[6:0]}), .out(adder_1_out));  // open: cin, cout
  assign d_bus = in_9 ? MH_q : 8'bz;  // Controlled_Buffer controlled_buffer_11
  assign a_bus = s_a ? {SH_q, SL_q} : 16'bz;  // Controlled_Buffer SA
  and and_6 (halt, IR_q[0], sel_dst[1], sel_dst[2], sel_dst[3], sel_src[0], sel_src[1], sel_src[2], sel_src[3]);
  Decoder #(.select(3)) decoder_1 (
    .out0(decoder_1_out0), .out1(decoder_1_out1), .out2(decoder_1_out2), .out3(decoder_1_out3),
    .out4(decoder_1_out4), .out5(decoder_1_out5), .out6(decoder_1_out6), .out7(decoder_1_out7),
    .sel(a_bus[2:0]), .en(and_5_out));
  Pull_Resistor pull_resistor_1 (.node(decoder_1_out0));
  Pull_Resistor pull_resistor_2 (.node(decoder_1_out2));
  Pull_Resistor pull_resistor_3 (.node(decoder_1_out1));
  Pull_Resistor pull_resistor_4 (.node(decoder_1_out3));
  Hex_Digit_Display hex_digit_display_6 (.value(a_bus[3:0]));  // open: dp
  Hex_Digit_Display hex_digit_display_7 (.value(SH_q[7:4]));  // open: dp
  or or_9 (sel_dst[0], word2, IR_q[0]);
  assign d_bus = and_7_out ? controlled_buffer_14_out : 8'bz;  // Controlled_Buffer controlled_buffer_12
  and and_7 (and_7_out, mr, sel_in);
  Pull_Resistor pull_resistor_5 (.node(decoder_1_out5));
  Pull_Resistor pull_resistor_6 (.node(decoder_1_out6));
  Pull_Resistor pull_resistor_7 (.node(decoder_1_out4));
  Pull_Resistor pull_resistor_8 (.node(decoder_1_out7));
  assign A_XL_out = sel_a_x ? XL_q : 8'bz;  // Controlled_Buffer A_XL
  assign A_XL_out = not_3_out ? YL_q : 8'bz;  // Controlled_Buffer A_YL
  not not_3 (not_3_out, sel_a_x);
  assign {B_XH_out_2, B_XH_out} = sel_a_x ? XH_q : 8'bz;  // Controlled_Buffer B_XH
  assign {B_XH_out_2, B_XH_out} = not_4_out ? YH_q : 8'bz;  // Controlled_Buffer B_YH
  not not_4 (not_4_out, sel_a_x);
  assign d_bus = in_10 ? register_5_q : 8'bz;  // Controlled_Buffer controlled_buffer_13
  Hex_Digit_Display hex_digit_display_8 (.value(SH_q[3:0]));  // open: dp
  assign controlled_buffer_14_out = decoder_2_out0 ? R_out : 8'bz;  // Controlled_Buffer controlled_buffer_14
  Decoder #(.select(3)) decoder_2 (
    .out0(decoder_2_out0), .sel(a_bus[2:0]), .en(undriven));  // open: out1, out2, out3, out4, out5, out6, out7
  Register register_1 (.D(d_bus), .Q(register_1_q), .clk(decoder_1_out0));  // open: en, clr
  Register register_2 (.D(d_bus), .Q(register_2_q), .clk(decoder_1_out2));  // open: en, clr
  Register register_3 (.D(d_bus), .Q(register_3_q), .clk(decoder_1_out4));  // open: en, clr
  Register register_4 (.D(d_bus), .Q(register_4_q), .clk(decoder_1_out6));  // open: en, clr
  Register register_5 (.D(d_bus), .Q(register_5_q), .clk(ld_alu_cmd));  // open: en, clr
  Button button_2 (.out(R_out[7]));
  Button button_3 (.out(R_out[5]));
  Button button_4 (.out(R_out[6]));
  Button button_5 (.out(R_out[4]));
  Hex_Digit_Display hex_digit_display_9 (.value(A_XL_out[3:0]));  // open: dp
  Hex_Digit_Display hex_digit_display_10 (.value(A_XL_out[7:4]));  // open: dp
  or or_10 (or_10_out, mr0, m_a0);
  or or_11 (or_11_out, inc_s, mr3);
  or or_12 (x_a, x_a0, x_a1);
  or or_13 (y_a, y_a0, y_a1);
  or or_14 (m_a, m_a0, m_a1);
  or or_15 (s_a, inc_s, s_a1);
  or or_16 (z_a, mr4, z_a1);
  Decoder #(.select(4)) decoder_3 (
    .out0(a_out), .out1(b_out), .out2(alu_out), .out3(mem_out), .out4(stk_out), .out5(lit_out),
    .out6(zm_out), .out12(dstk_out), .out13(dlit_out), .sel(sel_src));  // open: out7, out8, out9, out10, out11, out14, out15, en
  Register register_6 (.D(d_bus), .Q(register_6_q), .clk(decoder_1_out1));  // open: en, clr
  DotMatrix #(.inputtype("row"), .matrixcols(8), .matrixrows(8), .dotshape("circle")) dotmatrix_1 (
    .row0(register_1_q), .row1(register_6_q), .row2(register_2_q), .row3(register_7_q), .row4(register_3_q),
    .row5(register_8_q), .row6(register_4_q), .row7(register_9_q));
  Register register_7 (.D(d_bus), .Q(register_7_q), .clk(decoder_1_out3));  // open: en, clr
  Register register_8 (.D(d_bus), .Q(register_8_q), .clk(decoder_1_out5));  // open: en, clr
  Register register_9 (.D(d_bus), .Q(register_9_q), .clk(decoder_1_out7));  // open: en, clr
  Hex_Digit_Display hex_digit_display_11 (.value(B_XH_out_2));  // open: dp
  Register FLAG_Latch (
    .D({{5{1'b0}}, and_20_out[2], rom_2_data[5], and_20_out[0]}), .Q(FLAG_Latch_q), .clk(p0));  // open: en, clr
  or or_17 (or_17_out, or_10_out, or_11_out);
  or or_18 (mr, or_17_out, mr4);
  Button L (.out(R_out[2]));
  ROM #(.addrWidth(13)) rom_1 (
    .addr({FLAGS_q[1], register_5_q[3:0], B_XH_out, A_XL_out[3:0]}), .data(rom_1_data));  // open: sel
  ROM #(.addrWidth(13)) rom_2 (
    .addr({rom_1_data[5], register_5_q[3:0], B_XH_out_2, A_XL_out[7:4]}), .data(rom_2_data));  // open: sel
  Hex_Digit_Display hex_digit_display_12 (.value(B_XH_out));  // open: dp
  assign controlled_buffer_15_out = flags_in ? FLAG_Latch_q : 8'bz;  // Controlled_Buffer controlled_buffer_15
  Register FLAGS (.D(controlled_buffer_15_out), .Q(FLAGS_q), .clk(or_19_out));  // open: en, clr
  assign controlled_buffer_15_out = in_11 ? d_bus : 8'bz;  // Controlled_Buffer controlled_buffer_16
  or or_19 (or_19_out, in_11, flags_in);
  or or_20 (inc_x, inc_x0, inc_x1);
  or or_21 (inc_y, inc_y0, inc_y1);
  Button U (.out(R_out[1]));
  Button R (.out(R_out[0]));
  Button D (.out(R_out[3]));
  Hex_Digit_Display hex_digit_display_13 (.value(ALU_Latch_q_2));  // open: dp
  or or_22 (cond_true, or_23_out, and_21_out);
  and and_8 (and_8_out, or_33_out, a_out);
  Hex_Digit_Display hex_digit_display_14 (.value(ALU_Latch_q));  // open: dp
  assign d_bus = alu_d ? {ALU_Latch_q_2, ALU_Latch_q} : 8'bz;  // Controlled_Buffer controlled_buffer_17
  or or_23 (or_23_out, and_15_out, and_22_out);
  and and_9 (and_9_out, sel_ram, mr);
  and and_10 (and_10_out, sel_ram, mw);
  and and_11 (alu_d, or_33_out, alu_out);
  and and_12 (and_12_out, or_33_out, b_out);
  and and_13 (xl_d, and_8_out, sel_a_x);
  and and_14 (yl_d, and_8_out, nsel_a_x);
  Register ALU_Latch (
    .D({rom_2_data[3:0], rom_1_data[3:0]}), .Q({ALU_Latch_q_2, ALU_Latch_q}), .clk(p0));  // open: en, clr
  and and_15 (and_15_out, register_5_q[4], FLAGS_q[0]);
  assign d_bus = and_9_out ? controlled_buffer_19_out : 8'bz;  // Controlled_Buffer controlled_buffer_18
  assign controlled_buffer_19_out = and_10_out ? d_bus : 8'bz;  // Controlled_Buffer controlled_buffer_19
  not not_5 (not_5_out, and_10_out);
  and and_16 (inc_s, or_33_out, or_26_out);
  and and_17 (m_a0, or_33_out, mem_out);
  and and_18 (xh_d, and_12_out, sel_a_x);
  and and_19 (yh_d, and_12_out, nsel_a_x);
  or or_24 (or_24_out, toggle0, toggle1);
  and and_20 (and_20_out[0], rom_1_data[4], rom_2_data[4]);
  or or_25 (or_25_out, and_20_out[0], rom_2_data[5]);
  and and_21 (and_21_out, register_5_q[6], FLAGS_q[2]);
  and and_22 (and_22_out, register_5_q[5], FLAGS_q[1]);
  Decoder #(.select(4)) decoder_4 (
    .out0(a_in), .out1(b_in), .out2(ml_in), .out3(mh_in), .out4(sl_in), .out5(sh_in), .out6(mem_in),
    .out7(stk_in), .out8(aop_in), .out9(off_in), .out10(zl_in), .out11(zh_in), .out12(zm_in),
    .out13(decoder_4_out13), .out14(toggle_reg_cond), .out15(toggle_reg), .sel(sel_dst));  // open: en
  or or_26 (or_26_out, dstk_out, stk_out);
  or or_27 (or_27_out, dlit_out, lit_out);
  and and_23 (mr3, or_33_out, or_27_out);
  T_Flip_Flop t_ff_1 (.clk(or_24_out), .T(1'b1), .Q(sel_a_x));  // open: Qn, preset, reset, en
  not not_6 (and_20_out[2], or_25_out);
  RAM #(.addrWidth(15), .bus("asynch")) ram_1 (
    .addr(a_bus[14:0]), .data(controlled_buffer_19_out), .ld(not_5_out));  // open: sel, clr
  and and_24 (mr4, or_33_out, zm_out);
  and and_25 (x_a1, mr3, nsel_a_x);
  and and_26 (y_a1, mr3, sel_a_x);
  Clock clock_1 (.out(clock_1_out));
  not not_7 (not_7_out, NO_INT);
  Counter #(.width(2), .max('h3)) YH_2 (
    .count(1'b1), .Q(YH_2_q), .clk(or_28_out), .clr(button_1_out));  // open: load, D, carry
  or or_28 (or_28_out, halt, clock_1_out);
  D_Flip_Flop d_ff_1 (.clk(or_29_out), .D(not_7_out), .Q(d_ff_1_q[2]));  // open: Qn, preset, en, reset
  or or_29 (or_29_out, p0, decoder_5_out4);
  or or_30 (mr0, p0, decoder_5_out1);
  not not_8 (not_8_out, word2);
  or or_31 (or_31_out, dlit_out, lit_out);
  and and_27 (and_27_out, decoder_5_out3, or_31_out);
  Decoder #(.select(3)) decoder_5 (
    .out0(p0), .out1(decoder_5_out1), .out2(decoder_5_out2), .out3(decoder_5_out3), .out4(decoder_5_out4),
    .out7(decoder_5_out7), .sel({d_ff_1_q[2], YH_2_q}));  // open: out5, out6, en
  and and_28 (ld_ir, not_8_out, decoder_5_out1);
  and and_29 (dec_s, p0, stk_in);
  or or_32 (bit_dbl, dstk_out, dlit_out);
  and and_30 (inc_x1, and_27_out, not_9_out);
  not not_9 (not_9_out, sel_a_x);
  and and_31 (inc_y1, and_27_out, sel_a_x);
  or or_33 (or_33_out, decoder_5_out2, decoder_5_out3);
  and and_32 (flags_in, decoder_5_out3, alu_out);
  not not_10 (not_10_out, sel_a_x);
  not not_11 (not_11_out, sel_a_x);
  not not_12 (nsel_a_x, sel_a_x);
  and and_33 (x_a0, mr0, not_10_out);
  and and_34 (y_a0, mr0, sel_a_x);
  and and_35 (inc_x0, ld_ir, not_11_out);
  and and_36 (inc_y0, ld_ir, sel_a_x);
  not not_13 (not_13_out, decoder_5_out3);
  and and_37 (and_37_out, decoder_5_out3, a_in);
  S_R_Flip_Flop Single_Pulse (
    .S(decoder_6_out11), .clk(decoder_6_out11), .R(1'b0), .Q(Single_Pulse_q), .reset(Single_Pulse_q));  // open: Qn, preset, en
  T_Flip_Flop t_ff_2 (.clk(not_13_out), .T(bit_dbl), .Q(word2));  // open: Qn, preset, reset, en
  and and_38 (and_38_out, decoder_5_out3, b_in);
  and and_39 (ld_ml, decoder_5_out3, ml_in);
  and and_40 (ld_xl, and_37_out, sel_a_x);
  and and_41 (ld_yl, and_37_out, nsel_a_x);
  and and_42 (ld_mh, decoder_5_out3, mh_in);
  and and_43 (ld_xh, and_38_out, sel_a_x);
  and and_44 (ld_yh, and_38_out, nsel_a_x);
  and and_45 (and_45_out, INT_0, Single_Pulse_q);
  and and_46 (and_46_out, INT_1, Single_Pulse_q);
  and and_47 (and_47_out, INT_2, Single_Pulse_q);
  and and_48 (ld_sh, decoder_5_out3, sh_in);
  and and_49 (ld_sl, decoder_5_out3, sl_in);
  Register IntEn (.Q(IntEn_q));  // open: D, en, clk, clr
  Button button_6 (.out(button_6_out));
  Button button_7 (.out(button_7_out));
  Button button_8 (.out(button_8_out));
  Counter #(.width(4), .max('hf)) counter_1 (
    .count(decoder_5_out7), .Q(counter_1_q), .clk(decoder_5_out7), .clr(decoder_6_out11));  // open: load, D, carry
  or or_34 (or_34_out, and_45_out, button_6_out);
  or or_35 (or_35_out, and_46_out, button_7_out);
  or or_36 (or_36_out, and_47_out, button_8_out);
  Decoder #(.select(4)) decoder_6 (
    .out11(decoder_6_out11), .sel(counter_1_q));  // open: out0, out1, out2, out3, out4, out5, out6, out7, out8, out9, out10, out12, out13, out14, out15, en
  and and_50 (ld_alu_cmd, decoder_5_out3, aop_in);
  and and_51 (and_51_out, IntEn_q[0], button_6_out);
  and and_52 (and_52_out, IntEn_q[0], button_7_out);
  and and_53 (and_53_out, IntEn_q[0], button_8_out);
  and and_54 (and_54_out, decoder_5_out3, toggle_reg_cond);
  and and_55 (toggle0, decoder_5_out3, toggle_reg);
  and and_56 (ld_off, decoder_5_out3, off_in);
  and and_57 (ld_zl, decoder_5_out3, zl_in);
  and and_58 (toggle1, and_54_out, cond_true);
  S_R_Flip_Flop IntPend0 (
    .S(and_51_out), .clk(or_34_out), .R(and_45_out), .Q(IntPend0_q[0]));  // open: Qn, preset, reset, en
  S_R_Flip_Flop IntPend1 (
    .S(and_52_out), .clk(or_35_out), .R(and_46_out), .Q(IntPend0_q[1]));  // open: Qn, preset, reset, en
  S_R_Flip_Flop IntPend2 (
    .S(and_53_out), .clk(or_36_out), .R(and_47_out), .Q(IntPend0_q[2]));  // open: Qn, preset, reset, en
  and and_59 (ld_zh, decoder_5_out3, zh_in);
  Decoder #(.select(3)) decoder_7 (
    .out0(NO_INT), .out1(decoder_7_out1), .out2(decoder_7_out2), .out3(decoder_7_out3), .out4(INT_2),
    .out5(decoder_7_out5), .out6(decoder_7_out6), .out7(decoder_7_out7), .sel(IntPend0_q));  // open: en
  or or_37 (or_37_out, zm_in, stk_in);
  or or_38 (or_38_out, or_37_out, mem_in);
  or or_39 (or_39_out, decoder_7_out1, decoder_7_out3);
  or or_40 (or_40_out, decoder_7_out5, decoder_7_out7);
  or or_41 (INT_1, decoder_7_out2, decoder_7_out6);
  // AND_Gate and_60 has open pins: in0=or_33_out, in1=a_in, out=open
  // AND_Gate and_61 has open pins: in0=or_33_out, in1=b_in, out=open
  and and_62 (mw, or_33_out, or_38_out);
  or or_42 (INT_0, or_39_out, or_40_out);
  // AND_Gate and_63 has open pins: in0=or_33_out, in1=ml_in, out=open
  // AND_Gate and_64 has open pins: in0=or_33_out, in1=mh_in, out=open
  // AND_Gate and_65 has open pins: in0=or_33_out, in1=sl_in, out=open
  and and_66 (m_a1, or_33_out, mem_in);
  // AND_Gate and_67 has open pins: in0=or_33_out, in1=sh_in, out=open
  and and_68 (s_a1, or_33_out, stk_in);
  // AND_Gate and_69 has open pins: in0=or_33_out, in1=aop_in, out=open
  // AND_Gate and_70 has open pins: in0=or_33_out, in1=toggle_reg, out=open
  and and_71 (z_a1, or_33_out, zm_in);

  // Other names for the same wires on the sheet: sel_io = a_bus[15]; alu_cmd_d = in_10; ld_flags = in_11; mh_d = in_9;
  //   ml_d = in_8; mr1 = m_a0; mr2 = inc_s; s_a0 = inc_s; sh_d = in_4; sl_d = in_3; z_a0 = mr4; zh_d = in_7;
  //   zl_d = in_6

  // Notes on the sheet:
  //   ++++++++++++++++++++++++++++
  //   Data bus
  //   Address bus
  //   Carry in
  //   carry
  //   ALU High
  //   ALU Low
  //   contents of rom_1 (hex, n*v repeats v):
  //   10 1 2 3 4 5 6 7 8 9 a b c d e f 1 2 3 4 5 6 7 8 9 a b c d e f 30 2 3 4 5 6 7 8 9 a b c d e f 30 21
  //   3 4 5 6 7 8 9 a b c d e f 30 21 22 4 5 6 7 8 9 a b c d e f 30 21 22 23 5 6 7 8 9 a b c d e f 30 21
  //   22 23 24 6 7 8 9 a b c d e f 30 21 22 23 24 25 7 8 9 a b c d e f 30 21 22 23 24 25 26 8 9 a b c d e
  //   f 30 21 22 23 24 25 26 27 9 a b c d e f 30 21 22 23 24 25 26 27 28 a b c d e f 30 21 22 23 24 25 26
  //   27 28 29 b c d e f 30 21 22 23 24 25 26 27 28 29 2a c d e f 30 21 22 23 24 25 26 27 28 29 2a 2b d e
  //   f 30 21 22 23 24 25 26 27 28 29 2a 2b 2c e f 30 21 22 23 24 25 26 27 28 29 2a 2b 2c 2d f 30 21 22 23
  //   24 25 26 27 28 29 2a 2b 2c 2d 2e 10 1 2 3 4 5 6 7 8 9 a b c d e f 2f 10 1 2 3 4 5 6 7 8 9 a b c d e
  //   2e 2f 10 1 2 3 4 5 6 7 8 9 a b c d 2d 2e 2f 10 1 2 3 4 5 6 7 8 9 a b c 2c 2d 2e 2f 10 1 2 3 4 5 6 7
  //   8 9 a b 2b 2c 2d 2e 2f 10 1 2 3 4 5 6 7 8 9 a 2a 2b 2c 2d 2e 2f 10 1 2 3 4 5 6 7 8 9 29 2a 2b 2c 2d
  //   2e 2f 10 1 2 3 4 5 6 7 8 28 29 2a 2b 2c 2d 2e 2f 10 1 2 3 4 5 6 7 27 28 29 2a 2b 2c 2d 2e 2f 10 1 2
  //   3 4 5 6 26 27 28 29 2a 2b 2c 2d 2e 2f 10 1 2 3 4 5 25 26 27 28 29 2a 2b 2c 2d 2e 2f 10 1 2 3 4 24 25
  //   26 27 28 29 2a 2b 2c 2d 2e 2f 10 1 2 3 23 24 25 26 27 28 29 2a 2b 2c 2d 2e 2f 10 1 2 22 23 24 25 26
  //   27 28 29 2a 2b 2c 2d 2e 2f 10 1 21 22 23 24 25 26 27 28 29 2a 2b 2c 2d 2e 2f 10 10 2f 2e 2d 2c 2b 2a
  //   29 28 27 26 25 24 23 22 21 10 2f 2e 2d 2c 2b 2a 29 28 27 26 25 24 23 22 21 10 2f 2e 2d 2c 2b 2a 29
  //   28 27 26 25 24 23 22 21 10 2f 2e 2d 2c 2b 2a 29 28 27 26 25 24 23 22 21 10 2f 2e 2d 2c 2b 2a 29 28
  //   27 26 25 24 23 22 21 10 2f 2e 2d 2c 2b 2a 29 28 27 26 25 24 23 22 21 10 2f 2e 2d 2c 2b 2a 29 28 27
  //   26 25 24 23 22 21 10 2f 2e 2d 2c 2b 2a 29 28 27 26 25 24 23 22 21 10 2f 2e 2d 2c 2b 2a 29 28 27 26
  //   25 24 23 22 21 10 2f 2e 2d 2c 2b 2a 29 28 27 26 25 24 23 22 21 10 2f 2e 2d 2c 2b 2a 29 28 27 26 25
  //   24 23 22 21 10 2f 2e 2d 2c 2b 2a 29 28 27 26 25 24 23 22 21 10 2f 2e 2d 2c 2b 2a 29 28 27 26 25 24
  //   23 22 21 10 2f 2e 2d 2c 2b 2a 29 28 27 26 25 24 23 22 21 10 2f 2e 2d 2c 2b 2a 29 28 27 26 25 24 23
  //   22 21 10 2f 2e 2d 2c 2b 2a 29 28 27 26 25 24 23 22 21 10 2 4 6 8 a c e 30 22 24 26 28 2a 2c 2e 10 2
  //   4 6 8 a c e 30 22 24 26 28 2a 2c 2e 10 2 4 6 8 a c e 30 22 24 26 28 2a 2c 2e 10 2 4 6 8 a c e 30 22
  //   24 26 28 2a 2c 2e 10 2 4 6 8 a c e 30 22 24 26 28 2a 2c 2e 10 2 4 6 8 a c e 30 22 24 26 28 2a 2c 2e
  //   10 2 4 6 8 a c e 30 22 24 26 28 2a 2c 2e 10 2 4 6 8 a c e 30 22 24 26 28 2a 2c 2e 10 2 4 6 8 a c e
  //   30 22 24 26 28 2a 2c 2e 10 2 4 6 8 a c e 30 22 24 26 28 2a 2c 2e 10 2 4 6 8 a c e 30 22 24 26 28 2a
  //   2c 2e 10 2 4 6 8 a c e 30 22 24 26 28 2a 2c 2e 10 2 4 6 8 a c e 30 22 24 26 28 2a 2c 2e 10 2 4 6 8 a
  //   c e 30 22 24 26 28 2a 2c 2e 10 2 4 6 8 a c e 30 22 24 26 28 2a 2c 2e 10 2 4 6 8 a c e 30 22 24 26 28
  //   2a 2c 2e 256*10 1 2 3 4 5 6 7 8 9 a b c d e f 30 1 2 3 4 5 6 7 8 9 a b c d e f 30 1 2 3 4 5 6 7 8 9
  //   a b c d e f 30 1 2 3 4 5 6 7 8 9 a b c d e f 30 1 2 3 4 5 6 7 8 9 a b c d e f 30 1 2 3 4 5 6 7 8 9 a
  //   b c d e f 30 1 2 3 4 5 6 7 8 9 a b c d e f 30 1 2 3 4 5 6 7 8 9 a b c d e f 30 1 2 3 4 5 6 7 8 9 a b
  //   c d e f 30 1 2 3 4 5 6 7 8 9 a b c d e f 30 1 2 3 4 5 6 7 8 9 a b c d e f 30 1 2 3 4 5 6 7 8 9 a b c
  //   d e f 30 1 2 3 4 5 6 7 8 9 a b c d e f 30 1 2 3 4 5 6 7 8 9 a b c d e f 30 1 2 3 4 5 6 7 8 9 a b c d
  //   e f 30 1 2 3 4 5 6 7 8 9 a b c d e f 30 10 1 2 3 4 5 6 7 8 9 a b c d e f 1 2 3 4 5 6 7 8 9 a b c d e
  //   f 30 2 3 4 5 6 7 8 9 a b c d e f 30 21 3 4 5 6 7 8 9 a b c d e f 30 21 22 4 5 6 7 8 9 a b c d e f 30
  //   21 22 23 5 6 7 8 9 a b c d e f 30 21 22 23 24 6 7 8 9 a b c d e f 30 21 22 23 24 25 7 8 9 a b c d e
  //   f 30 21 22 23 24 25 26 8 9 a b c d e f 30 21 22 23 24 25 26 27 9 a b c d e f 30 21 22 23 24 25 26 27
  //   28 a b c d e f 30 21 22 23 24 25 26 27 28 29 b c d e f 30 21 22 23 24 25 26 27 28 29 2a c d e f 30
  //   21 22 23 24 25 26 27 28 29 2a 2b d e f 30 21 22 23 24 25 26 27 28 29 2a 2b 2c e f 30 21 22 23 24 25
  //   26 27 28 29 2a 2b 2c 2d f 30 21 22 23 24 25 26 27 28 29 2a 2b 2c 2d 2e 10 1 2 3 4 5 6 7 8 9 a b c d
  //   e f 2f 10 1 2 3 4 5 6 7 8 9 a b c d e 2e 2f 10 1 2 3 4 5 6 7 8 9 a b c d 2d 2e 2f 10 1 2 3 4 5 6 7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
  //   contents of rom_2 (hex, n*v repeats v):
  //   10 1 2 3 4 5 6 7 8 9 a b c d e f 1 2 3 4 5 6 7 8 9 a b c d e f 30 2 3 4 5 6 7 8 9 a b c d e f 30 21
  //   3 4 5 6 7 8 9 a b c d e f 30 21 22 4 5 6 7 8 9 a b c d e f 30 21 22 23 5 6 7 8 9 a b c d e f 30 21
  //   22 23 24 6 7 8 9 a b c d e f 30 21 22 23 24 25 7 8 9 a b c d e f 30 21 22 23 24 25 26 8 9 a b c d e
  //   f 30 21 22 23 24 25 26 27 9 a b c d e f 30 21 22 23 24 25 26 27 28 a b c d e f 30 21 22 23 24 25 26
  //   27 28 29 b c d e f 30 21 22 23 24 25 26 27 28 29 2a c d e f 30 21 22 23 24 25 26 27 28 29 2a 2b d e
  //   f 30 21 22 23 24 25 26 27 28 29 2a 2b 2c e f 30 21 22 23 24 25 26 27 28 29 2a 2b 2c 2d f 30 21 22 23
  //   24 25 26 27 28 29 2a 2b 2c 2d 2e 10 1 2 3 4 5 6 7 8 9 a b c d e f 2f 10 1 2 3 4 5 6 7 8 9 a b c d e
  //   2e 2f 10 1 2 3 4 5 6 7 8 9 a b c d 2d 2e 2f 10 1 2 3 4 5 6 7 8 9 a b c 2c 2d 2e 2f 10 1 2 3 4 5 6 7
  //   8 9 a b 2b 2c 2d 2e 2f 10 1 2 3 4 5 6 7 8 9 a 2a 2b 2c 2d 2e 2f 10 1 2 3 4 5 6 7 8 9 29 2a 2b 2c 2d
  //   2e 2f 10 1 2 3 4 5 6 7 8 28 29 2a 2b 2c 2d 2e 2f 10 1 2 3 4 5 6 7 27 28 29 2a 2b 2c 2d 2e 2f 10 1 2
  //   3 4 5 6 26 27 28 29 2a 2b 2c 2d 2e 2f 10 1 2 3 4 5 25 26 27 28 29 2a 2b 2c 2d 2e 2f 10 1 2 3 4 24 25
  //   26 27 28 29 2a 2b 2c 2d 2e 2f 10 1 2 3 23 24 25 26 27 28 29 2a 2b 2c 2d 2e 2f 10 1 2 22 23 24 25 26
  //   27 28 29 2a 2b 2c 2d 2e 2f 10 1 21 22 23 24 25 26 27 28 29 2a 2b 2c 2d 2e 2f 10 10 2f 2e 2d 2c 2b 2a
  //   29 28 27 26 25 24 23 22 21 10 2f 2e 2d 2c 2b 2a 29 28 27 26 25 24 23 22 21 10 2f 2e 2d 2c 2b 2a 29
  //   28 27 26 25 24 23 22 21 10 2f 2e 2d 2c 2b 2a 29 28 27 26 25 24 23 22 21 10 2f 2e 2d 2c 2b 2a 29 28
  //   27 26 25 24 23 22 21 10 2f 2e 2d 2c 2b 2a 29 28 27 26 25 24 23 22 21 10 2f 2e 2d 2c 2b 2a 29 28 27
  //   26 25 24 23 22 21 10 2f 2e 2d 2c 2b 2a 29 28 27 26 25 24 23 22 21 10 2f 2e 2d 2c 2b 2a 29 28 27 26
  //   25 24 23 22 21 10 2f 2e 2d 2c 2b 2a 29 28 27 26 25 24 23 22 21 10 2f 2e 2d 2c 2b 2a 29 28 27 26 25
  //   24 23 22 21 10 2f 2e 2d 2c 2b 2a 29 28 27 26 25 24 23 22 21 10 2f 2e 2d 2c 2b 2a 29 28 27 26 25 24
  //   23 22 21 10 2f 2e 2d 2c 2b 2a 29 28 27 26 25 24 23 22 21 10 2f 2e 2d 2c 2b 2a 29 28 27 26 25 24 23
  //   22 21 10 2f 2e 2d 2c 2b 2a 29 28 27 26 25 24 23 22 21 10 2 4 6 8 a c e 30 22 24 26 28 2a 2c 2e 10 2
  //   4 6 8 a c e 30 22 24 26 28 2a 2c 2e 10 2 4 6 8 a c e 30 22 24 26 28 2a 2c 2e 10 2 4 6 8 a c e 30 22
  //   24 26 28 2a 2c 2e 10 2 4 6 8 a c e 30 22 24 26 28 2a 2c 2e 10 2 4 6 8 a c e 30 22 24 26 28 2a 2c 2e
  //   10 2 4 6 8 a c e 30 22 24 26 28 2a 2c 2e 10 2 4 6 8 a c e 30 22 24 26 28 2a 2c 2e 10 2 4 6 8 a c e
  //   30 22 24 26 28 2a 2c 2e 10 2 4 6 8 a c e 30 22 24 26 28 2a 2c 2e 10 2 4 6 8 a c e 30 22 24 26 28 2a
  //   2c 2e 10 2 4 6 8 a c e 30 22 24 26 28 2a 2c 2e 10 2 4 6 8 a c e 30 22 24 26 28 2a 2c 2e 10 2 4 6 8 a
  //   c e 30 22 24 26 28 2a 2c 2e 10 2 4 6 8 a c e 30 22 24 26 28 2a 2c 2e 10 2 4 6 8 a c e 30 22 24 26 28
  //   2a 2c 2e 257*10 1 2 3 4 5 6 7 8 9 a b c d e f 10 1 2 3 4 5 6 7 8 9 a b c d e f 10 1 2 3 4 5 6 7 8 9
  //   a b c d e f 10 1 2 3 4 5 6 7 8 9 a b c d e f 10 1 2 3 4 5 6 7 8 9 a b c d e f 10 1 2 3 4 5 6 7 8 9 a
  //   b c d e f 10 1 2 3 4 5 6 7 8 9 a b c d e f 10 1 2 3 4 5 6 7 8 9 a b c d e f 10 1 2 3 4 5 6 7 8 9 a b
  //   c d e f 10 1 2 3 4 5 6 7 8 9 a b c d e f 10 1 2 3 4 5 6 7 8 9 a b c d e f 10 1 2 3 4 5 6 7 8 9 a b c
  //   d e f 10 1 2 3 4 5 6 7 8 9 a b c d e f 10 1 2 3 4 5 6 7 8 9 a b c d e f 10 1 2 3 4 5 6 7 8 9 a b c d
  //   e f 10 1 2 3 4 5 6 7 8 9 a b c d e f 10 1 2 3 4 5 6 7 8 9 a b c d e f 1 2 3 4 5 6 7 8 9 a b c d e f
  //   30 2 3 4 5 6 7 8 9 a b c d e f 30 21 3 4 5 6 7 8 9 a b c d e f 30 21 22 4 5 6 7 8 9 a b c d e f 30
  //   21 22 23 5 6 7 8 9 a b c d e f 30 21 22 23 24 6 7 8 9 a b c d e f 30 21 22 23 24 25 7 8 9 a b c d e
  //   f 30 21 22 23 24 25 26 8 9 a b c d e f 30 21 22 23 24 25 26 27 9 a b c d e f 30 21 22 23 24 25 26 27
  //   28 a b c d e f 30 21 22 23 24 25 26 27 28 29 b c d e f 30 21 22 23 24 25 26 27 28 29 2a c d e f 30
  //   21 22 23 24 25 26 27 28 29 2a 2b d e f 30 21 22 23 24 25 26 27 28 29 2a 2b 2c e f 30 21 22 23 24 25
  //   26 27 28 29 2a 2b 2c 2d f 30 21 22 23 24 25 26 27 28 29 2a 2b 2c 2d 2e 10 1 2 3 4 5 6 7 8 9 a b c d
  //   e f 2f 10 1 2 3 4 5 6 7 8 9 a b c d e 2e 2f 10 1 2 3 4 5 6 7 8 9 a b c d 2d 2e 2f 10 1 2 3 4 5 6 7 8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
  //   carry_out
  //   zero_low
  //   zero_high
  //   =
  //   <
  //   >
  //   Deferred SP decrement to p0
endmodule
