// Digital circuit decode.dig as structural Verilog
module decode (
  input  RST,
  input  [7:0] DATA,
  input  clk,
  input  C,
  input  Z,
  input  SF,
  input  OF,
  input  INT,
  output b_o,
  output sh_o,
  output sl_o,
  output mh_o,
  output ml_o,
  output off_o,
  output s_a,
  output alu_d,
  output mf_a,
  output aluf_d,
  output f_o,
  output NC,
  output b_i,
  output sh_i,
  output sl_i,
  output mh_i,
  output ml_i,
  output off_i,
  output sl,
  output sl_plus__plus,
  output NC1,
  output f_i,
  output NC2,
  output A_i,
  output A_o,
  output MREAD,
  output MWRITE,
  output pAh_o,
  output pAl_o,
  output pAh_i,
  output pAl_i,
  output pBc_plus__plus,
  output pBc_a,
  output pBh_o,
  output pBl_o,
  output pBh_i,
  output pBl_i,
  output pAc_plus__plus,
  output pAc_a,
  output [15:0] Address,
  output [4:0] ALU_op,
  output ALU_latch,
  output ei,
  output s_rst,
  output di_iv_o,
  output [7:0] DBG,
  output FAULT,
  output sel_high,
  output sel_A
);

  wire _7400_1_pin5, _7400_1_pin6, _7400_2_pin3, _7400_2_pin10, _7432_1_pin3, _7432_1_pin6, _7432_1_pin8,
       _7432_1_pin11, _7432_2_pin3, _7432_2_pin6, _7432_2_pin8, _7432_2_pin11, _7432_3_pin4, _7432_3_pin6,
       _7432_3_pin8, _7432_3_pin10, _7432_5_pin3, _7432_5_pin11, _7432_7_pin3, _7432_7_pin11, _74138_1_pin7,
       _74138_1_pin11, _74138_1_pin12, _74138_1_pin13, _74138_1_pin14, _74138_1_pin15, _74138_2_pin7,
       _74138_2_pin9, _74138_2_pin10, _74138_3_pin7, _74138_3_pin15, _74138_4_pin7, _74138_4_pin9,
       _74138_4_pin10, _74138_4_pin12, _74138_4_pin15, _74138_5_pin7, _74138_5_pin9, _74138_5_pin11,
       _74138_5_pin12, _74138_5_pin15, _74138_6_pin7, _74138_6_pin9, _74138_6_pin10, _74138_6_pin11,
       _74138_6_pin12, _74138_6_pin13, _74138_6_pin14, _74138_6_pin15, _74138_7_pin7, _74138_7_pin9,
       _74138_7_pin10, _74138_7_pin11, _74138_7_pin12, _74138_7_pin13, _74138_7_pin14, _74138_7_pin15,
       _74138_8_pin7, _74138_8_pin9, _74138_8_pin10, _74138_8_pin11, _74138_8_pin12, _74138_8_pin13,
       _74138_8_pin14, _74138_8_pin15, _74138_9_pin7, _74138_9_pin9, _74138_9_pin10, _74138_9_pin11,
       _74138_9_pin12, _74138_9_pin13, _74138_9_pin14, _74138_9_pin15, _74161_1_pin7, _74161_2_pin11,
       _74161_2_pin12, _74161_2_pin13, _74161_2_pin14, _74541_1_pin19, _74541_3_pin19, _74573_1_pin11,
       _74573_2_pin2, _74573_2_pin3, _74573_2_pin4, _74573_2_pin5, and_1_out, and_2_out, and_3_out,
       and_4_out, and_5_out, and_6_out, and_7_out, and_8_out, and_9_out, and_10_out, and_11_out, and_12_out,
       and_13_out, and_14_out, and_15_out, and_17_out, and_18_out, nor_1_out, not_1_out, not_2_out,
       not_3_out, not_4_out, not_6_out, not_16_out, or_1_out, or_2_out, or_3_out, or_4_out, or_5_out,
       or_6_out, or_7_out, or_8_out, or_9_out, xor_1_out, xor_2_out, xor_3_out, xor_4_out, xor_5_out,
       xor_6_out;
  wire [3:0] _74573_2_pin16;
  wire [7:0] CONTROL_high_d, CONTROL_low_d;

  _7432 _7432_1 (
    .pin1(DATA[7]), .pin2(INT), .pin3(_7432_1_pin3), .pin4(DATA[6]), .pin5(INT), .pin6(_7432_1_pin6),
    .pin7(1'b0), .pin8(_7432_1_pin8), .pin9(DATA[3]), .pin10(INT), .pin11(_7432_1_pin11), .pin12(DATA[2]),
    .pin13(INT), .pin14(1'b1));
  _7432 _7432_2 (
    .pin1(DATA[5]), .pin2(INT), .pin3(_7432_2_pin3), .pin4(DATA[4]), .pin5(INT), .pin6(_7432_2_pin6),
    .pin7(1'b0), .pin8(_7432_2_pin8), .pin9(DATA[0]), .pin10(INT), .pin11(_7432_2_pin11), .pin12(DATA[1]),
    .pin13(INT), .pin14(1'b1));
  xor xor_1 (xor_1_out, SF, OF);
  or or_1 (or_1_out, xor_1_out, Z);
  or or_2 (or_2_out, Z, C);
  xor xor_2 (xor_2_out, ALU_op[3], Z);
  xor xor_3 (xor_3_out, ALU_op[3], C);
  xor xor_4 (xor_4_out, ALU_op[3], or_1_out);
  xor xor_5 (xor_5_out, ALU_op[3], or_2_out);
  xor xor_6 (xor_6_out, ALU_op[3], xor_1_out);
  _74573 _74573_1 (
    .pin1(1'b0), .pin2(_7432_2_pin8), .pin3(_7432_2_pin11), .pin4(_7432_1_pin11), .pin5(_7432_1_pin8),
    .pin6(_7432_2_pin6), .pin7(_7432_2_pin3), .pin8(_7432_1_pin6), .pin9(_7432_1_pin3), .pin10(1'b0),
    .pin11(_74573_1_pin11), .pin12(DBG[7]), .pin13(DBG[6]), .pin14(DBG[5]), .pin15(ALU_op[4]),
    .pin16(ALU_op[3]), .pin17(ALU_op[2]), .pin18(ALU_op[1]), .pin19(ALU_op[0]), .pin20(1'b1));
  or or_3 (or_3_out, _74138_1_pin11, xor_6_out);
  and and_1 (and_1_out, or_3_out, _74138_1_pin7);
  or or_4 (or_4_out, _74138_1_pin12, xor_5_out);
  and and_2 (and_2_out, and_4_out, and_1_out);
  not not_1 (not_1_out, clk);
  or or_5 (or_5_out, _74138_1_pin13, xor_4_out);
  and and_3 (and_3_out, or_5_out, or_4_out);
  _74138 _74138_1 (
    .pin1(ALU_op[0]), .pin2(ALU_op[1]), .pin3(ALU_op[2]), .pin4(1'b0), .pin5(1'b0), .pin6(1'b1),
    .pin7(_74138_1_pin7), .pin8(1'b0), .pin11(_74138_1_pin11), .pin12(_74138_1_pin12),
    .pin13(_74138_1_pin13), .pin14(_74138_1_pin14), .pin15(_74138_1_pin15), .pin16(1'b1));  // open: pin9, pin10
  or or_6 (or_6_out, _74138_1_pin14, xor_3_out);
  and and_4 (and_4_out, and_5_out, and_3_out);
  or or_7 (or_7_out, _74138_1_pin15, xor_2_out);
  and and_5 (and_5_out, or_7_out, or_6_out);
  _74573 _74573_2 (
    .pin1(1'b0), .pin2(_74573_2_pin2), .pin3(_74573_2_pin3), .pin4(_74573_2_pin4), .pin5(_74573_2_pin5),
    .pin6(1'b0), .pin7(1'b0), .pin8(1'b0), .pin9(1'b0), .pin10(1'b0), .pin11(not_1_out),
    .pin16(_74573_2_pin16[3]), .pin17(_74573_2_pin16[2]), .pin18(_74573_2_pin16[1]),
    .pin19(_74573_2_pin16[0]), .pin20(1'b1));  // open: pin12, pin13, pin14, pin15
  or or_8 (or_8_out, and_9_out, RST);
  not not_2 (not_2_out, or_8_out);
  _74161 _74161_1 (
    .pin1(not_2_out), .pin2(clk), .pin3(1'b0), .pin4(1'b0), .pin5(1'b0), .pin6(1'b0), .pin7(_74161_1_pin7),
    .pin8(1'b0), .pin9(1'b1), .pin10(_74161_1_pin7), .pin11(_74573_2_pin5), .pin12(_74573_2_pin4),
    .pin13(_74573_2_pin3), .pin14(_74573_2_pin2), .pin16(1'b1));  // open: pin15
  _74161 _74161_2 (
    .pin1(not_2_out), .pin2(clk), .pin3(1'b0), .pin4(1'b0), .pin5(1'b0), .pin6(1'b0), .pin7(1'b1),
    .pin8(1'b0), .pin9(1'b1), .pin10(1'b1), .pin11(_74161_2_pin11), .pin12(_74161_2_pin12),
    .pin13(_74161_2_pin13), .pin14(_74161_2_pin14), .pin15(_74161_1_pin7), .pin16(1'b1));
  and and_6 (and_6_out, _74161_2_pin14, _74161_2_pin13);
  and and_7 (and_7_out, _74161_2_pin12, _74161_2_pin11);
  ROM #(.AddrBits(13), .isProgramMemory("true"), .Bits(8)) CONTROL_low (
    .A({1'b0, DBG[7:5], ALU_op, _74573_2_pin16}), .sel(or_9_out), .D(CONTROL_low_d));
  ROM #(.AddrBits(13), .isProgramMemory("true"), .Bits(8)) CONTROL_high (
    .A({1'b0, DBG[7:5], ALU_op, _74573_2_pin16}), .sel(or_9_out),
    .D({CONTROL_high_d[7], sel_high, CONTROL_high_d[5], sel_A, CONTROL_high_d[3:0]}));
  and and_8 (and_8_out, and_6_out, and_7_out);
  or or_9 (or_9_out, _74161_2_pin12, _74161_2_pin11);
  not not_3 (not_3_out, and_8_out);
  PullDown pulldown_1 (.out(CONTROL_high_d[0]));
  PullDown pulldown_2 (.out(CONTROL_high_d[1]));
  PullDown pulldown_3 (.out(CONTROL_high_d[2]));
  PullDown pulldown_4 (.out(CONTROL_high_d[3]));
  not not_4 (not_4_out, sel_A);
  not not_5 (di_iv_o, CONTROL_high_d[5]);
  PullDown pulldown_5 (.out(sel_A));
  PullDown pulldown_6 (.out(CONTROL_high_d[5]));
  PullDown pulldown_7 (.out(sel_high));
  PullDown pulldown_8 (.out(CONTROL_high_d[7]));
  _74541 _74541_1 (
    .pin1(1'b0), .pin2(ALU_op[0]), .pin3(ALU_op[1]), .pin4(ALU_op[2]), .pin5(ALU_op[3]), .pin6(ALU_op[4]),
    .pin7(1'b0), .pin8(1'b1), .pin9(1'b1), .pin10(1'b0), .pin11(Address[7]), .pin12(Address[6]),
    .pin13(Address[5]), .pin14(Address[4]), .pin15(Address[3]), .pin16(Address[2]), .pin17(Address[1]),
    .pin18(Address[0]), .pin19(_74541_1_pin19), .pin20(1'b1));
  _74541 _74541_2 (
    .pin1(not_4_out), .pin2(CONTROL_low_d[0]), .pin3(CONTROL_low_d[1]), .pin4(1'b1), .pin5(1'b1),
    .pin6(1'b1), .pin7(1'b1), .pin8(1'b0), .pin9(1'b1), .pin10(1'b0), .pin11(Address[7]), .pin12(Address[6]),
    .pin13(Address[5]), .pin14(Address[4]), .pin15(Address[3]), .pin16(Address[2]), .pin17(Address[1]),
    .pin18(Address[0]), .pin19(1'b0), .pin20(1'b1));
  PullDown pulldown_9 (.out(CONTROL_low_d[0]));
  PullDown pulldown_10 (.out(CONTROL_low_d[1]));
  PullDown pulldown_11 (.out(CONTROL_low_d[2]));
  PullDown pulldown_12 (.out(CONTROL_low_d[3]));
  not not_6 (not_6_out, CONTROL_high_d[7]);
  PullDown pulldown_13 (.out(CONTROL_low_d[4]));
  PullDown pulldown_14 (.out(CONTROL_low_d[5]));
  PullDown pulldown_15 (.out(CONTROL_low_d[6]));
  PullDown pulldown_16 (.out(CONTROL_low_d[7]));
  and and_9 (and_9_out, and_8_out, CONTROL_low_d[7]);
  and and_10 (and_10_out, and_7_out, not_3_out);
  and and_11 (and_11_out, _74161_2_pin11, not_3_out);
  and and_12 (and_12_out, CONTROL_low_d[5], and_10_out);
  and and_13 (and_13_out, CONTROL_low_d[6], and_10_out);
  and and_14 (and_14_out, CONTROL_low_d[5], and_10_out);
  and and_15 (and_15_out, CONTROL_low_d[6], and_10_out);
  and and_16 (A_i, CONTROL_high_d[0], and_10_out);
  and and_17 (and_17_out, and_11_out, CONTROL_high_d[2]);
  and and_18 (and_18_out, CONTROL_high_d[3], and_10_out);
  or or_10 (ALU_latch, and_9_out, not_16_out);
  _74541 _74541_3 (
    .pin1(1'b0), .pin2(1'b1), .pin3(1'b1), .pin4(1'b1), .pin5(1'b1), .pin6(1'b1), .pin7(1'b1), .pin8(1'b1),
    .pin9(1'b1), .pin10(1'b0), .pin11(Address[15]), .pin12(Address[14]), .pin13(Address[13]),
    .pin14(Address[12]), .pin15(Address[11]), .pin16(Address[10]), .pin17(Address[9]), .pin18(Address[8]),
    .pin19(_74541_3_pin19), .pin20(1'b1));
  _74138 _74138_2 (
    .pin1(CONTROL_low_d[0]), .pin2(CONTROL_low_d[1]), .pin3(CONTROL_low_d[2]), .pin4(CONTROL_high_d[7]),
    .pin5(1'b0), .pin6(CONTROL_low_d[3]), .pin7(_74138_2_pin7), .pin8(1'b0), .pin9(_74138_2_pin9),
    .pin10(_74138_2_pin10), .pin11(ml_o), .pin12(mh_o), .pin13(sl_o), .pin14(sh_o), .pin15(b_o), .pin16(1'b1));
  _74138 _74138_3 (
    .pin1(CONTROL_low_d[0]), .pin2(CONTROL_low_d[1]), .pin3(CONTROL_low_d[2]), .pin4(CONTROL_high_d[7]),
    .pin5(1'b0), .pin6(CONTROL_low_d[4]), .pin7(_74138_3_pin7), .pin8(1'b0), .pin9(_74541_1_pin19),
    .pin10(f_o), .pin11(aluf_d), .pin12(mf_a), .pin13(alu_d), .pin14(s_a), .pin15(_74138_3_pin15),
    .pin16(1'b1));
  _74138 _74138_4 (
    .pin1(CONTROL_low_d[0]), .pin2(CONTROL_low_d[1]), .pin3(CONTROL_low_d[2]), .pin4(CONTROL_high_d[7]),
    .pin5(1'b0), .pin6(and_12_out), .pin7(_74138_4_pin7), .pin8(1'b0), .pin9(_74138_4_pin9),
    .pin10(_74138_4_pin10), .pin11(ml_i), .pin12(_74138_4_pin12), .pin13(sl_i), .pin14(sh_i),
    .pin15(_74138_4_pin15), .pin16(1'b1));
  _74138 _74138_5 (
    .pin1(CONTROL_low_d[0]), .pin2(CONTROL_low_d[1]), .pin3(CONTROL_low_d[2]), .pin4(CONTROL_high_d[7]),
    .pin5(1'b0), .pin6(and_13_out), .pin7(_74138_5_pin7), .pin8(1'b0), .pin9(_74138_5_pin9), .pin10(mh_i),
    .pin11(_74138_5_pin11), .pin12(_74138_5_pin12), .pin13(sl_plus__plus), .pin14(sl),
    .pin15(_74138_5_pin15), .pin16(1'b1));
  _74138 _74138_6 (
    .pin1(CONTROL_low_d[0]), .pin2(CONTROL_low_d[1]), .pin3(CONTROL_low_d[2]), .pin4(not_6_out), .pin5(1'b0),
    .pin6(CONTROL_low_d[3]), .pin7(_74138_6_pin7), .pin8(1'b0), .pin9(_74138_6_pin9), .pin10(_74138_6_pin10),
    .pin11(_74138_6_pin11), .pin12(_74138_6_pin12), .pin13(_74138_6_pin13), .pin14(_74138_6_pin14),
    .pin15(_74138_6_pin15), .pin16(1'b1));
  _74138 _74138_7 (
    .pin1(CONTROL_low_d[0]), .pin2(CONTROL_low_d[1]), .pin3(CONTROL_low_d[2]), .pin4(not_6_out), .pin5(1'b0),
    .pin6(CONTROL_low_d[4]), .pin7(_74138_7_pin7), .pin8(1'b0), .pin9(_74138_7_pin9), .pin10(_74138_7_pin10),
    .pin11(_74138_7_pin11), .pin12(_74138_7_pin12), .pin13(_74138_7_pin13), .pin14(_74138_7_pin14),
    .pin15(_74138_7_pin15), .pin16(1'b1));
  _74138 _74138_8 (
    .pin1(CONTROL_low_d[0]), .pin2(CONTROL_low_d[1]), .pin3(CONTROL_low_d[2]), .pin4(not_6_out), .pin5(1'b0),
    .pin6(and_14_out), .pin7(_74138_8_pin7), .pin8(1'b0), .pin9(_74138_8_pin9), .pin10(_74138_8_pin10),
    .pin11(_74138_8_pin11), .pin12(_74138_8_pin12), .pin13(_74138_8_pin13), .pin14(_74138_8_pin14),
    .pin15(_74138_8_pin15), .pin16(1'b1));
  _74138 _74138_9 (
    .pin1(CONTROL_low_d[0]), .pin2(CONTROL_low_d[1]), .pin3(CONTROL_low_d[2]), .pin4(not_6_out), .pin5(1'b0),
    .pin6(and_15_out), .pin7(_74138_9_pin7), .pin8(1'b0), .pin9(_74138_9_pin9), .pin10(_74138_9_pin10),
    .pin11(_74138_9_pin11), .pin12(_74138_9_pin12), .pin13(_74138_9_pin13), .pin14(_74138_9_pin14),
    .pin15(_74138_9_pin15), .pin16(1'b1));
  and and_19 (_74541_3_pin19, _74541_1_pin19, not_4_out);
  not not_7 (_74573_1_pin11, _74138_5_pin15);
  not not_8 (off_i, _74138_4_pin15);
  not not_9 (b_i, _74138_4_pin12);
  not not_10 (ei, _74138_4_pin10);
  not not_11 (s_rst, _74138_5_pin12);
  not not_12 (f_i, _74138_5_pin11);
  not not_13 (A_o, CONTROL_high_d[1]);
  not not_14 (MREAD, and_17_out);
  not not_15 (MWRITE, and_18_out);
  not not_16 (not_16_out, _74138_2_pin10);
  nor nor_1 (nor_1_out, _74138_5_pin7, and_2_out);
  _7432 _7432_3 (
    .pin1(1'b0), .pin2(1'b0), .pin4(_7432_3_pin4), .pin5(nor_1_out), .pin6(_7432_3_pin6), .pin7(1'b0),
    .pin8(_7432_3_pin8), .pin9(nor_1_out), .pin10(_7432_3_pin10), .pin12(1'b1), .pin13(1'b1), .pin14(1'b1));  // open: pin3, pin11
  _7400 _7400_1 (
    .pin1(1'b0), .pin2(1'b0), .pin4(_7432_3_pin6), .pin5(_7400_1_pin5), .pin6(_7400_1_pin6), .pin7(1'b0),
    .pin8(_7400_1_pin5), .pin9(_7400_1_pin6), .pin10(_7432_3_pin8), .pin12(1'b1), .pin13(1'b1), .pin14(1'b1));  // open: pin3, pin11
  _7400 _7400_2 (
    .pin1(nor_1_out), .pin2(_7400_1_pin6), .pin3(_7400_2_pin3), .pin4(_7400_2_pin3), .pin5(_7432_3_pin10),
    .pin6(_7432_3_pin4), .pin7(1'b0), .pin8(_7432_3_pin10), .pin9(_7432_3_pin4), .pin10(_7400_2_pin10),
    .pin11(_7400_2_pin10), .pin12(_7400_1_pin5), .pin13(nor_1_out), .pin14(1'b1));
  _7432 _7432_4 (
    .pin1(_7432_3_pin10), .pin2(_74138_4_pin9), .pin3(pAh_i), .pin4(_7432_3_pin10), .pin5(_74138_4_pin7),
    .pin6(pAl_i), .pin7(1'b0), .pin8(pAl_o), .pin9(_74138_2_pin7), .pin10(_7432_3_pin10), .pin11(pAh_o),
    .pin12(_7432_3_pin10), .pin13(_74138_2_pin9), .pin14(1'b1));
  _7432 _7432_5 (
    .pin1(_7432_3_pin4), .pin2(_74138_3_pin7), .pin3(_7432_5_pin3), .pin4(1'b0), .pin5(1'b0), .pin7(1'b0),
    .pin8(pBc_plus__plus), .pin9(_7432_3_pin10), .pin10(_74138_5_pin9), .pin11(_7432_5_pin11),
    .pin12(_7432_3_pin10), .pin13(_74138_3_pin15), .pin14(1'b1));  // open: pin6
  _7432 _7432_6 (
    .pin1(_7432_3_pin4), .pin2(_74138_4_pin9), .pin3(pBh_i), .pin4(_7432_3_pin4), .pin5(_74138_4_pin7),
    .pin6(pBl_i), .pin7(1'b0), .pin8(pBl_o), .pin9(_74138_2_pin7), .pin10(_7432_3_pin4), .pin11(pBh_o),
    .pin12(_74138_2_pin9), .pin13(_7432_3_pin4), .pin14(1'b1));
  _7432 _7432_7 (
    .pin1(_7432_3_pin10), .pin2(_74138_3_pin7), .pin3(_7432_7_pin3), .pin4(1'b0), .pin5(1'b0), .pin7(1'b0),
    .pin8(pAc_plus__plus), .pin9(_7432_3_pin4), .pin10(_74138_5_pin9), .pin11(_7432_7_pin11),
    .pin12(_7432_3_pin4), .pin13(_74138_3_pin15), .pin14(1'b1));  // open: pin6
  and and_20 (pBc_a, _7432_5_pin11, _7432_5_pin3);
  and and_21 (pAc_a, _7432_7_pin11, _7432_7_pin3);

  assign DBG[4:0] = ALU_op;
  assign FAULT = 1'b0;
  assign NC = 1'b0;
  assign NC1 = 1'b0;
  assign NC2 = 1'b0;
  assign off_o = 1'b1;

  // Notes on the sheet:
  //   clk: Hz: 2
  //   SF=OF
  //   (active low)
  //   (SF=OF && ZF = 0)
  //   (active low)
  //   (CF=0 && ZF = 0)
  //   (active low)
  //   zero if condition met
  //   CONTROL_low loads microcode_0.bin.hex
  //   CONTROL_high loads microcode_1.bin.hex
  //   cword enable
  //   seq rst request
  //   seq reset
  //   Phase write
  //   Phase mread
  //   PC switch toggle logic
endmodule
