// Digital circuit interrupt.dig as structural Verilog
module interrupt (
  input  in_1,
  input  in_2,
  input  in_3,
  input  in_4,
  input  in_5,
  input  P0,
  input  in_7
);

  wire _74573_1_pin16, _74573_1_pin17, _74573_1_pin18, _74573_1_pin19, and_1_out, and_2_out, and_3_out,
       and_4_out, and_5_out, and_6_out, and_7_out, nor_1_out, nor_2_out, nor_3_out, nor_4_out, nor_5_out,
       nor_6_out, nor_7_out, nor_8_out, not_1_out, not_2_out, not_3_out, or_1_out, or_2_out, or_3_out,
       or_4_out, or_5_out, or_6_out;

  and and_1 (and_1_out, _74573_1_pin19, in_3);
  and and_2 (and_2_out, _74573_1_pin18, in_3);
  and and_3 (and_3_out, _74573_1_pin17, in_3);
  and and_4 (and_4_out, _74573_1_pin16, in_3);
  or or_1 (or_1_out, and_1_out, in_7);
  or or_2 (or_2_out, and_2_out, in_7);
  or or_3 (or_3_out, and_3_out, in_7);
  or or_4 (or_4_out, and_4_out, in_7);
  nor nor_1 (nor_1_out, or_1_out, nor_2_out);
  nor nor_2 (nor_2_out, nor_1_out, in_1);
  nor nor_3 (nor_3_out, or_2_out, nor_4_out);
  nor nor_4 (nor_4_out, nor_3_out, in_2);
  nor nor_5 (nor_5_out, or_3_out, nor_6_out);
  nor nor_6 (nor_6_out, nor_5_out, in_4);
  nor nor_7 (nor_7_out, or_4_out, nor_8_out);
  nor nor_8 (nor_8_out, nor_7_out, in_5);
  not not_1 (not_1_out, nor_1_out);
  and and_5 (and_5_out, not_1_out, nor_3_out);
  or or_5 (or_5_out, nor_1_out, nor_3_out);
  not not_2 (not_2_out, or_5_out);
  and and_6 (and_6_out, not_2_out, nor_5_out);
  or or_6 (or_6_out, or_5_out, nor_5_out);
  not not_3 (not_3_out, or_6_out);
  and and_7 (and_7_out, not_3_out, nor_7_out);
  _74573 _74573_1 (
    .pin1(1'b0), .pin2(nor_1_out), .pin3(and_5_out), .pin4(and_6_out), .pin5(and_7_out), .pin6(1'b0),
    .pin7(1'b0), .pin8(1'b0), .pin9(1'b0), .pin10(1'b0), .pin11(P0), .pin16(_74573_1_pin16),
    .pin17(_74573_1_pin17), .pin18(_74573_1_pin18), .pin19(_74573_1_pin19), .pin20(1'b1));  // open: pin12, pin13, pin14, pin15
endmodule
