// Digital circuit mar.dig as structural Verilog
module mar (
  input  LOW_D,
  input  HIGH_D,
  input  MF_A,
  input  LOW_LD,
  input  HIGH_LD,
  input  INC,
  input  DEC,
  input  RST,
  input  [7:0] DATA,
  input  OFF_i,
  input  OFF_o,
  input  off_im,
  input  [4:0] imm,
  output [7:0] DATA_OUT,
  output [15:0] Address
);

  wire _7483_1_pin2, _7483_1_pin6, _7483_1_pin9, _7483_1_pin14, _7483_1_pin15, _7483_2_pin2, _7483_2_pin6,
       _7483_2_pin9, _7483_2_pin14, _7483_2_pin15, _7483_3_pin2, _7483_3_pin6, _7483_3_pin9, _7483_3_pin14,
       _7483_3_pin15, _7483_4_pin2, _7483_4_pin6, _7483_4_pin9, _7483_4_pin14, _7483_4_pin15, _74193_1_pin2,
       _74193_1_pin3, _74193_1_pin6, _74193_1_pin7, _74193_1_pin12, _74193_1_pin13, _74193_2_pin2,
       _74193_2_pin3, _74193_2_pin6, _74193_2_pin7, _74193_2_pin12, _74193_2_pin13, _74193_3_pin2,
       _74193_3_pin3, _74193_3_pin6, _74193_3_pin7, _74193_3_pin12, _74193_3_pin13, _74193_4_pin2,
       _74193_4_pin3, _74193_4_pin6, _74193_4_pin7, _74573_1_pin12, _74573_1_pin13, _74573_1_pin14,
       _74573_1_pin15, _74573_1_pin16, _74573_1_pin17, _74573_1_pin18, _74573_1_pin19, _74573_2_pin15,
       _74573_2_pin16, _74573_2_pin17, _74573_2_pin18, _74573_2_pin19, not_1_out;

  not not_1 (not_1_out, off_im);
  _74573 _74573_1 (
    .pin1(not_1_out), .pin2(imm[0]), .pin3(imm[1]), .pin4(imm[2]), .pin5(imm[3]), .pin6(imm[4]),
    .pin7(imm[4]), .pin8(imm[4]), .pin9(imm[4]), .pin10(1'b0), .pin11(1'b1), .pin12(_74573_1_pin12),
    .pin13(_74573_1_pin13), .pin14(_74573_1_pin14), .pin15(_74573_1_pin15), .pin16(_74573_1_pin16),
    .pin17(_74573_1_pin17), .pin18(_74573_1_pin18), .pin19(_74573_1_pin19), .pin20(1'b1));
  _74573 _74573_2 (
    .pin1(1'b0), .pin2(DATA[0]), .pin3(DATA[1]), .pin4(DATA[2]), .pin5(DATA[3]), .pin6(DATA[4]),
    .pin7(DATA[5]), .pin8(DATA[6]), .pin9(DATA[7]), .pin10(1'b0), .pin11(OFF_i), .pin15(_74573_2_pin15),
    .pin16(_74573_2_pin16), .pin17(_74573_2_pin17), .pin18(_74573_2_pin18), .pin19(_74573_2_pin19),
    .pin20(1'b1));  // open: pin12, pin13, pin14
  _74193 _74193_1 (
    .pin1(DATA[1]), .pin2(_74193_1_pin2), .pin3(_74193_1_pin3), .pin4(DEC), .pin5(INC), .pin6(_74193_1_pin6),
    .pin7(_74193_1_pin7), .pin8(1'b0), .pin9(DATA[3]), .pin10(DATA[2]), .pin11(HIGH_LD),
    .pin12(_74193_1_pin12), .pin13(_74193_1_pin13), .pin14(RST), .pin15(DATA[0]), .pin16(1'b1));
  _74193 _74193_2 (
    .pin1(DATA[5]), .pin2(_74193_2_pin2), .pin3(_74193_2_pin3), .pin4(_74193_1_pin13), .pin5(_74193_1_pin12),
    .pin6(_74193_2_pin6), .pin7(_74193_2_pin7), .pin8(1'b0), .pin9(DATA[7]), .pin10(DATA[6]),
    .pin11(HIGH_LD), .pin12(_74193_2_pin12), .pin13(_74193_2_pin13), .pin14(RST), .pin15(DATA[4]),
    .pin16(1'b1));
  _74541 _74541_1 (
    .pin1(1'b0), .pin2(_74573_2_pin19), .pin3(_74573_2_pin18), .pin4(_74573_2_pin17), .pin5(_74573_2_pin16),
    .pin6(_74573_2_pin15), .pin7(1'b0), .pin8(1'b1), .pin9(1'b1), .pin10(1'b0), .pin11(Address[7]),
    .pin12(Address[6]), .pin13(Address[5]), .pin14(Address[4]), .pin15(Address[3]), .pin16(Address[2]),
    .pin17(Address[1]), .pin18(Address[0]), .pin19(MF_A), .pin20(1'b1));
  _74541 _74541_2 (
    .pin1(1'b0), .pin2(1'b1), .pin3(1'b1), .pin4(1'b1), .pin5(1'b1), .pin6(1'b1), .pin7(1'b1), .pin8(1'b1),
    .pin9(1'b1), .pin10(1'b0), .pin11(Address[15]), .pin12(Address[14]), .pin13(Address[13]),
    .pin14(Address[12]), .pin15(Address[11]), .pin16(Address[10]), .pin17(Address[9]), .pin18(Address[8]),
    .pin19(MF_A), .pin20(1'b1));
  _74541 _74541_3 (
    .pin1(1'b0), .pin2(_74193_1_pin3), .pin3(_74193_1_pin2), .pin4(_74193_1_pin6), .pin5(_74193_1_pin7),
    .pin6(_74193_2_pin3), .pin7(_74193_2_pin2), .pin8(_74193_2_pin6), .pin9(_74193_2_pin7), .pin10(1'b0),
    .pin11(DATA_OUT[7]), .pin12(DATA_OUT[6]), .pin13(DATA_OUT[5]), .pin14(DATA_OUT[4]), .pin15(DATA_OUT[3]),
    .pin16(DATA_OUT[2]), .pin17(DATA_OUT[1]), .pin18(DATA_OUT[0]), .pin19(HIGH_D), .pin20(1'b1));
  _74193 _74193_3 (
    .pin1(DATA[1]), .pin2(_74193_3_pin2), .pin3(_74193_3_pin3), .pin4(_74193_2_pin13), .pin5(_74193_2_pin12),
    .pin6(_74193_3_pin6), .pin7(_74193_3_pin7), .pin8(1'b0), .pin9(DATA[3]), .pin10(DATA[2]), .pin11(LOW_LD),
    .pin12(_74193_3_pin12), .pin13(_74193_3_pin13), .pin14(RST), .pin15(DATA[0]), .pin16(1'b1));
  _74193 _74193_4 (
    .pin1(DATA[5]), .pin2(_74193_4_pin2), .pin3(_74193_4_pin3), .pin4(_74193_3_pin13), .pin5(_74193_3_pin12),
    .pin6(_74193_4_pin6), .pin7(_74193_4_pin7), .pin8(1'b0), .pin9(DATA[7]), .pin10(DATA[6]), .pin11(LOW_LD),
    .pin14(RST), .pin15(DATA[4]), .pin16(1'b1));  // open: pin12, pin13
  _74541 _74541_4 (
    .pin1(1'b0), .pin2(_74193_3_pin3), .pin3(_74193_3_pin2), .pin4(_74193_3_pin6), .pin5(_74193_3_pin7),
    .pin6(_74193_4_pin3), .pin7(_74193_4_pin2), .pin8(_74193_4_pin6), .pin9(_74193_4_pin7), .pin10(1'b0),
    .pin11(DATA_OUT[7]), .pin12(DATA_OUT[6]), .pin13(DATA_OUT[5]), .pin14(DATA_OUT[4]), .pin15(DATA_OUT[3]),
    .pin16(DATA_OUT[2]), .pin17(DATA_OUT[1]), .pin18(DATA_OUT[0]), .pin19(LOW_D), .pin20(1'b1));
  _7483 _7483_1 (
    .pin1(_74193_3_pin7), .pin2(_7483_1_pin2), .pin3(_74193_3_pin6), .pin4(_74573_1_pin17), .pin5(1'b1),
    .pin6(_7483_1_pin6), .pin7(_74573_1_pin18), .pin8(_74193_3_pin2), .pin9(_7483_1_pin9),
    .pin10(_74193_3_pin3), .pin11(_74573_1_pin19), .pin12(1'b0), .pin13(1'b0), .pin14(_7483_1_pin14),
    .pin15(_7483_1_pin15), .pin16(_74573_1_pin16));
  _7483 _7483_2 (
    .pin1(_74193_4_pin7), .pin2(_7483_2_pin2), .pin3(_74193_4_pin6), .pin4(_74573_1_pin13), .pin5(1'b1),
    .pin6(_7483_2_pin6), .pin7(_74573_1_pin14), .pin8(_74193_4_pin2), .pin9(_7483_2_pin9),
    .pin10(_74193_4_pin3), .pin11(_74573_1_pin15), .pin12(1'b0), .pin13(_7483_1_pin14),
    .pin14(_7483_2_pin14), .pin15(_7483_2_pin15), .pin16(_74573_1_pin12));
  _7483 _7483_3 (
    .pin1(_74193_1_pin7), .pin2(_7483_3_pin2), .pin3(_74193_1_pin6), .pin4(_74573_1_pin12), .pin5(1'b1),
    .pin6(_7483_3_pin6), .pin7(_74573_1_pin12), .pin8(_74193_1_pin2), .pin9(_7483_3_pin9),
    .pin10(_74193_1_pin3), .pin11(_74573_1_pin12), .pin12(1'b0), .pin13(_7483_2_pin14),
    .pin14(_7483_3_pin14), .pin15(_7483_3_pin15), .pin16(_74573_1_pin12));
  _7483 _7483_4 (
    .pin1(_74193_2_pin7), .pin2(_7483_4_pin2), .pin3(_74193_2_pin6), .pin4(_74573_1_pin12), .pin5(1'b1),
    .pin6(_7483_4_pin6), .pin7(_74573_1_pin12), .pin8(_74193_2_pin2), .pin9(_7483_4_pin9),
    .pin10(_74193_2_pin3), .pin11(_74573_1_pin12), .pin12(1'b0), .pin13(_7483_3_pin14),
    .pin14(_7483_4_pin14), .pin15(_7483_4_pin15), .pin16(_74573_1_pin12));
  _74541 _74541_5 (
    .pin1(1'b0), .pin2(_7483_1_pin9), .pin3(_7483_1_pin6), .pin4(_7483_1_pin2), .pin5(_7483_1_pin15),
    .pin6(_7483_2_pin9), .pin7(_7483_2_pin6), .pin8(_7483_2_pin2), .pin9(_7483_2_pin15), .pin10(1'b0),
    .pin11(Address[7]), .pin12(Address[6]), .pin13(Address[5]), .pin14(Address[4]), .pin15(Address[3]),
    .pin16(Address[2]), .pin17(Address[1]), .pin18(Address[0]), .pin19(not_1_out), .pin20(1'b1));
  _74541 _74541_6 (
    .pin1(1'b0), .pin2(_7483_3_pin9), .pin3(_7483_3_pin6), .pin4(_7483_3_pin2), .pin5(_7483_3_pin15),
    .pin6(_7483_4_pin9), .pin7(_7483_4_pin6), .pin8(_7483_4_pin2), .pin9(_7483_4_pin15), .pin10(1'b0),
    .pin11(Address[15]), .pin12(Address[14]), .pin13(Address[13]), .pin14(Address[12]), .pin15(Address[11]),
    .pin16(Address[10]), .pin17(Address[9]), .pin18(Address[8]), .pin19(not_1_out), .pin20(1'b1));

  // Notes on the sheet:
  //   LOW_D: default 1
  //   HIGH_D: default 1
  //   MF_A: default 1
  //   LOW_LD: default 1
  //   HIGH_LD: default 1
  //   OFF_o: default 1
  //   Switch to common registers from counters
endmodule
